// Logisim project Main Circuit.circ as structural Verilog: 3 circuits, main circuit part-1
// ALU
module part_1 (
  input  Clock,
  input  [7:0] A,
  input  [7:0] B,
  input  Clear,
  input  [3:0] FunSel,
  output [7:0] OutALU,
  output [3:0] ZCNO
);

  wire adder_1_cout, adder_2_cout, adder_3_cout, and_2_out, main_1_carry_out, main_2_overflow,
       main_3_carry_out, main_3_overflow, multiplexer_1_out, multiplexer_2_out, multiplexer_4_out, not_4_out,
       not_5_out, Overflow_Checker_2_overflowout, Overflow_Checker_3_overflowout,
       Overflow_Checker_overflowout, Zero_Output_Checker_out;
  wire [7:0] adder_1_out, adder_2_out, adder_3_out, and_1_out, main_1_output, main_2_output, main_3_output,
       not_1_out, not_2_out, not_3_out, or_1_out, xor_1_out;

  Hex_Digit_Display hex_digit_display_1 (.value(A[3:0]));  // open: dp
  Hex_Digit_Display hex_digit_display_2 (.value(A[7:4]));  // open: dp
  Hex_Digit_Display hex_digit_display_3 (.value(B[7:4]));  // open: dp
  Hex_Digit_Display hex_digit_display_4 (.value(B[3:0]));  // open: dp
  assign not_1_out = ~B;  // NOT_Gate not_1, 8 bits wide
  assign not_2_out = ~A;  // NOT_Gate not_2, 8 bits wide
  assign not_3_out = ~B;  // NOT_Gate not_3, 8 bits wide
  Adder adder_1 (.a(A), .b(B), .out(adder_1_out), .cin(1'b0), .cout(adder_1_cout));
  Adder adder_2 (.a(A), .b(B), .out(adder_2_out), .cin(ZCNO[2]), .cout(adder_2_cout));
  Adder adder_3 (.a(A), .b(not_1_out), .out(adder_3_out), .cin(1'b1), .cout(adder_3_cout));
  assign and_1_out = A & B;  // AND_Gate and_1, 8 bits wide
  assign or_1_out = A | B;  // OR_Gate or_1, 8 bits wide
  assign xor_1_out = A ^ B;  // XOR_Gate xor_1, 8 bits wide
  Logical_Shift_main main_1 (.Input(A), .Left_Right(FunSel[0]), .Carry_Out(main_1_carry_out), .Output(main_1_output));
  Arithmetic_Shift_main main_2 (.Input(A), .Left_Right(FunSel[0]), .Output(main_2_output), .Overflow(main_2_overflow));
  circular_shift_main main_3 (
    .Input(A), .Carry_In(ZCNO[2]), .Left_Right(FunSel[0]), .Carry_Out(main_3_carry_out),
    .Output(main_3_output), .Overflow(main_3_overflow));
  OverflowChecker_main Overflow_Checker (
    .Funsel(FunSel), .OverflowOut(Overflow_Checker_overflowout), .Output(adder_1_out), .A(A), .B(B));
  OverflowChecker_main Overflow_Checker_2 (
    .Funsel(FunSel), .OverflowOut(Overflow_Checker_2_overflowout), .Output(adder_2_out), .A(A), .B(A));
  OverflowChecker_main Overflow_Checker_3 (
    .Funsel(FunSel), .OverflowOut(Overflow_Checker_3_overflowout), .Output(adder_3_out), .A(A), .B(B));
  Multiplexer #(.select(4), .enable("false")) multiplexer_1 (
    .in0(ZCNO[2]), .in1(ZCNO[2]), .in2(ZCNO[2]), .in3(ZCNO[2]), .in4(adder_1_cout), .in5(adder_2_cout),
    .in6(adder_3_cout), .in7(ZCNO[2]), .in8(ZCNO[2]), .in9(ZCNO[2]), .in10(main_1_carry_out),
    .in11(main_1_carry_out), .in12(ZCNO[2]), .in13(ZCNO[2]), .in14(main_3_carry_out),
    .in15(main_3_carry_out), .out(multiplexer_1_out), .sel(FunSel));
  Multiplexer #(.select(4), .enable("false")) multiplexer_2 (
    .in0(ZCNO[0]), .in1(ZCNO[0]), .in2(ZCNO[0]), .in3(ZCNO[0]), .in4(Overflow_Checker_overflowout),
    .in5(Overflow_Checker_2_overflowout), .in6(Overflow_Checker_3_overflowout), .in7(ZCNO[0]), .in8(ZCNO[0]),
    .in9(ZCNO[0]), .in10(ZCNO[0]), .in11(ZCNO[0]), .in12(main_2_overflow), .in13(ZCNO[0]),
    .in14(main_3_overflow), .in15(main_3_overflow), .out(multiplexer_2_out), .sel(FunSel));
  Multiplexer #(.select(4), .width(8), .enable("false")) multiplexer_3 (
    .in0(A), .in1(B), .in2(not_2_out), .in3(not_3_out), .in4(adder_1_out), .in5(adder_2_out),
    .in6(adder_3_out), .in7(and_1_out), .in8(or_1_out), .in9(xor_1_out), .in10(main_1_output),
    .in11(main_1_output), .in12(main_2_output), .in13(main_2_output), .in14(main_3_output),
    .in15(main_3_output), .out(OutALU), .sel(FunSel));
  not not_4 (not_4_out, Zero_Output_Checker_out);
  D_Flip_Flop Z (.clk(Clock), .D(not_4_out), .Q(ZCNO[3]), .en(1'b1), .reset(Clear));  // open: Qn, preset
  or Zero_Output_Checker (Zero_Output_Checker_out, OutALU[0], OutALU[1], OutALU[2], OutALU[3], OutALU[4], OutALU[5], OutALU[6], OutALU[7]);
  D_Flip_Flop C (.clk(Clock), .D(multiplexer_1_out), .Q(ZCNO[2]), .en(1'b1), .reset(Clear));  // open: Qn, preset
  Hex_Digit_Display hex_digit_display_5 (.value(OutALU[7:4]));  // open: dp
  D_Flip_Flop N (.clk(Clock), .D(multiplexer_4_out), .Q(ZCNO[1]), .en(1'b1), .reset(Clear));  // open: Qn, preset
  Hex_Digit_Display hex_digit_display_6 (.value(OutALU[3:0]));  // open: dp
  D_Flip_Flop O (.clk(Clock), .D(multiplexer_2_out), .Q(ZCNO[0]), .en(1'b1), .reset(Clear));  // open: Qn, preset
  not not_5 (not_5_out, FunSel[1]);
  and and_2 (and_2_out, FunSel[3], FunSel[2], not_5_out, FunSel[0]);
  Multiplexer #(.enable("false")) multiplexer_4 (
    .in0(OutALU[7]), .in1(ZCNO[1]), .out(multiplexer_4_out), .sel(and_2_out));

  // Notes on the sheet:
  //   A
  //   B
  //   Logical Shift
  //   Arithmetic Shift
  //   Circular Shift
endmodule

module part_2 (
  input  Clear,
  output [7:0] out_2,
  output [3:0] out_3,
  output [1:0] out_4,
  output [7:0] out_5,
  output [2:0] out_6,
  output [1:0] out_7,
  output [7:0] IR_8_15,
  output [7:0] IR_0_7
);

  wire Clock_out, IR_Enable, IR_LH, MuxCSel, RAM_Load, RAM_Store;
  wire [1:0] IR_Funsel, MuxASel, MuxBSel, OutAsel, OutBsel, OutCsel, OutDsel;
  wire [3:0] ALU_Funsel, ZCNO;
  wire [7:0] Address_Register_File_outc, Address_Register_File_outd, multiplexer_3_out, part_1_1_outalu,
       ram_1_data, Register_File_outa, Register_File_outb;

  Hex_Digit_Display hex_digit_display_1 (.value(IR_0_7[3:0]));  // open: dp
  Hex_Digit_Display hex_digit_display_2 (.value(IR_0_7[7:4]));  // open: dp
  Multiplexer #(.select(2), .width(8), .enable("false")) multiplexer_1 (
    .in0(IR_0_7), .in1(ram_1_data), .in2(Address_Register_File_outc), .in3(part_1_1_outalu), .out(out_2),
    .sel(MuxASel));
  Part_2a Register_File (
    .\input (out_2), .Clock(Clock_out), .OutASel(OutAsel), .OutBSel(OutBsel), .RegSel(out_3), .FunSel(out_4),
    .OutA(Register_File_outa), .OutB(Register_File_outb));
  Part_2c IR (
    .Input(ram_1_data), .Low_High(IR_LH), .Enable(IR_Enable), .IRout({IR_8_15, IR_0_7}), .FunSel(IR_Funsel),
    .Clock(Clock_out));
  Multiplexer #(.select(2), .width(8), .enable("false")) multiplexer_2 (
    .in1(IR_0_7), .in2(ram_1_data), .in3(part_1_1_outalu), .out(out_5), .sel(MuxBSel));  // open: in0
  Multiplexer #(.width(8), .enable("false")) multiplexer_3 (
    .in0(Address_Register_File_outc), .in1(Register_File_outa), .out(multiplexer_3_out), .sel(MuxCSel));
  Part_2b Address_Register_File (
    .\input (out_5), .Clock(Clock_out), .OutCSel(OutCsel), .OutDSel(OutDsel), .RegSel(out_6), .FunSel(out_7),
    .OutC(Address_Register_File_outc), .OutD(Address_Register_File_outd));
  Hex_Digit_Display hex_digit_display_3 (.value(IR_8_15[7:4]));  // open: dp
  Hex_Digit_Display hex_digit_display_4 (.value(IR_8_15[3:0]));  // open: dp
  Clock Clock (.out(Clock_out));
  part_1 part_1_1 (
    .Clock(Clock_out), .A(multiplexer_3_out), .B(Register_File_outb), .ZCNO(ZCNO), .FunSel(ALU_Funsel),
    .Clear(Clear), .OutALU(part_1_1_outalu));
  RAM #(.bus("separate")) ram_1 (
    .addr(Address_Register_File_outd), .din(part_1_1_outalu), .data(ram_1_data), .str(RAM_Store),
    .clk(Clock_out), .ld(RAM_Load));  // open: sel, clr
  control_unit Control_Unit (
    .Address_Regsel(out_6), .Address_Funsel(out_7), .Register_Regsel(out_3), .Register_Funsel(out_4),
    .RAM_Store(RAM_Store), .RAM_Load(RAM_Load), .MuxAsel(MuxASel), .MuxBsel(MuxBSel), .MuxCSel(MuxCSel),
    .OutDSel(OutDsel), .Clock(Clock_out), .IR_Funsel(IR_Funsel), .IR_Enable(IR_Enable), .IR_LH(IR_LH),
    .IR_8_15(IR_8_15), .IR_0_7(IR_0_7), .ALU_Funsel(ALU_Funsel), .ZCNO(ZCNO), .OutAsel(OutAsel),
    .OutBsel(OutBsel), .OutCSel(OutCsel));

  // Other names for the same wires on the sheet: Address_Funsel[1:0] = out_7; Address_Regsel[2:0] = out_6;
  //   Register_Funsel[1:0] = out_4; Register_Regsel[3:0] = out_3
endmodule

module control_unit (
  input  [7:0] IR_8_15,
  input  [7:0] IR_0_7,
  input  [3:0] ZCNO,
  input  Clock,
  output [1:0] IR_Funsel,
  output [2:0] Address_Regsel,
  output IR_Enable,
  output [1:0] Address_Funsel,
  output IR_LH,
  output [3:0] Register_Regsel,
  output [1:0] Register_Funsel,
  output RAM_Store,
  output [3:0] ALU_Funsel,
  output RAM_Load,
  output [1:0] MuxAsel,
  output [1:0] OutAsel,
  output [1:0] MuxBsel,
  output [1:0] OutBsel,
  output MuxCSel,
  output [1:0] OutCSel,
  output [1:0] OutDSel
);

  wire and_1_out, and_2_out, and_3_out, Condition, decoder_1_out2, decoder_1_out3, decoder_1_out4,
       decoder_1_out5, decoder_1_out7, decoder_1_out8, decoder_1_out9, decoder_1_out10, decoder_1_out11,
       decoder_1_out12, decoder_1_out13, decoder_2_out1, F1_1, F1_2, F1_3, F1_4, F1_5, F1_6, F1_7, F2_1,
       F2_2, F2_3, F2_4, F2_5, F2_6, F2_7, INC_DEC, multiplexer_5_out, multiplexer_6_out, not_1_out,
       not_2_out, not_3_out, not_4_out, not_6_out, Opcode_Type, or_2_out, Regsel_Enable, Source_Type, Sub,
       Z_Update;
  wire [0:0] multiplexer_25_out;
  wire [1:0] Branch, CD, controlled_buffer_3_out, multiplexer_2_out, multiplexer_4_out, multiplexer_7_out,
       multiplexer_8_out, multiplexer_11_out, multiplexer_12_out, multiplexer_13_out, multiplexer_14_out,
       multiplexer_16_out, multiplexer_18_out, multiplexer_19_out, multiplexer_20_out, multiplexer_21_out,
       multiplexer_27_out;
  wire [2:0] F1, F2, multiplexer_3_out, multiplexer_10_out;
  wire [3:0] multiplexer_1_out, multiplexer_9_out, ZCNO_Reg;
  wire [7:0] adder_1_out, Address, controlled_buffer_6_out, CSAR_q, multiplexer_24_out, multiplexer_26_out,
       OpcodeMapPlace, SBR_q;
  wire [28:0] rom_2_data;

  Multiplexer #(.select(2), .width(4), .enable("false")) multiplexer_1 (
    .in0(4'b0001), .in1(4'b0010), .in2(4'b0100), .in3(4'b1000), .out(multiplexer_1_out),
    .sel(multiplexer_2_out));
  Multiplexer #(.width(2), .enable("false")) multiplexer_2 (
    .in0(IR_8_15[2:1]), .in1(IR_8_15[1:0]), .out(multiplexer_2_out), .sel(Opcode_Type));
  Multiplexer #(.select(2), .width(3), .enable("false")) multiplexer_3 (
    .in0(3'b001), .in1(3'b001), .in2(3'b010), .in3(3'b100), .out(multiplexer_3_out), .sel(multiplexer_2_out));
  nor nor_1 (Source_Type, IR_0_7[7], IR_0_7[4]);
  Decoder #(.select(5), .disabled(0), .enable("false")) decoder_1 (
    .out2(decoder_1_out2), .out3(decoder_1_out3), .out4(decoder_1_out4), .out5(decoder_1_out5), .out6(Sub),
    .out7(decoder_1_out7), .out8(decoder_1_out8), .out9(decoder_1_out9), .out10(decoder_1_out10),
    .out11(decoder_1_out11), .out12(decoder_1_out12), .out13(decoder_1_out13), .sel(IR_8_15[7:3]));  // open: out0, out1, out14, out15, out16, out17, out18, out19, out20, out21, out22, out23, out24, out25, out26, out27, out28, out29, out30, out31
  Multiplexer #(.select(2), .width(2), .enable("false")) multiplexer_4 (
    .in0(2'b00), .in1(2'b01), .in2(2'b10), .in3(2'b11), .out(multiplexer_4_out), .sel(IR_0_7[6:5]));
  Multiplexer #(.enable("false")) multiplexer_5 (
    .in0(1'b0), .in1(IR_8_15[2]), .out(multiplexer_5_out), .sel(Opcode_Type));
  Multiplexer #(.enable("false")) multiplexer_6 (
    .in0(1'b0), .in1(IR_8_15[2]), .out(multiplexer_6_out), .sel(Opcode_Type));
  Register #(.width(4)) register_1 (.D(ZCNO), .en(Z_Update), .Q(ZCNO_Reg), .clk(Clock));  // open: clr
  Multiplexer #(.select(2), .width(2), .enable("false")) multiplexer_7 (
    .in0(2'b00), .in1(2'b01), .in2(2'b10), .in3(2'b11), .out(multiplexer_7_out), .sel(IR_0_7[3:2]));
  Multiplexer #(.select(2), .width(2), .enable("false")) multiplexer_8 (
    .in0(2'b00), .in1(2'b01), .in2(2'b10), .in3(2'b11), .out(multiplexer_8_out), .sel(IR_0_7[3:2]));
  Multiplexer #(.width(4), .enable("false")) multiplexer_9 (
    .in0(multiplexer_1_out), .in1(4'b0000), .out(multiplexer_9_out), .sel(multiplexer_5_out));
  Multiplexer #(.width(3), .enable("false")) multiplexer_10 (
    .in0(3'b000), .in1(multiplexer_3_out), .out(multiplexer_10_out), .sel(multiplexer_6_out));
  Multiplexer #(.width(2), .enable("false")) multiplexer_11 (
    .in0(multiplexer_4_out), .in1(multiplexer_7_out), .out(multiplexer_11_out), .sel(IR_0_7[7]));
  Multiplexer #(.select(2), .width(2), .enable("false")) multiplexer_12 (
    .in0(2'b00), .in1(2'b00), .in2(2'b01), .in3(2'b10), .out(multiplexer_12_out), .sel(IR_0_7[3:2]));
  assign Register_Regsel = Regsel_Enable ? multiplexer_9_out : 4'bz;  // Controlled_Buffer controlled_buffer_1
  assign Address_Regsel = Regsel_Enable ? multiplexer_10_out : 3'bz;  // Controlled_Buffer controlled_buffer_2
  or or_1 (Opcode_Type, decoder_1_out2, decoder_1_out3, decoder_1_out4, decoder_1_out5, Sub, decoder_1_out7, decoder_1_out8, decoder_1_out9, decoder_1_out10, decoder_1_out11, decoder_1_out12, decoder_1_out13);
  or or_2 (or_2_out, decoder_1_out7, decoder_1_out8);
  Multiplexer #(.width(2), .enable("false")) multiplexer_13 (
    .in0(multiplexer_11_out), .in1(multiplexer_8_out), .out(multiplexer_13_out), .sel(Source_Type));
  Multiplexer #(.select(2), .width(2), .enable("false")) multiplexer_14 (
    .in0(2'b00), .in1(2'b00), .in2(2'b01), .in3(2'b10), .out(multiplexer_14_out), .sel(IR_0_7[6:5]));
  and and_1 (and_1_out, Source_Type, Opcode_Type);
  not not_1 (not_1_out, IR_8_15[2]);
  Multiplexer #(.enable("false")) multiplexer_15 (.in0(1'b0), .in1(or_2_out), .out(INC_DEC), .sel(F1_2));
  Multiplexer #(.width(2), .enable("false")) multiplexer_16 (
    .in0(multiplexer_12_out), .in1(multiplexer_14_out), .out(multiplexer_16_out), .sel(IR_0_7[7]));
  Multiplexer #(.enable("false")) multiplexer_17 (.in0(and_1_out), .in1(not_1_out), .out(MuxCSel), .sel(INC_DEC));
  Multiplexer #(.select(2), .width(2), .enable("false")) multiplexer_18 (
    .in0(2'b00), .in1(2'b01), .in2(2'b10), .in3(2'b11), .out(multiplexer_18_out), .sel(IR_0_7[6:5]));
  Multiplexer #(.width(2), .enable("false")) multiplexer_19 (
    .in0(IR_8_15[2:1]), .in1(multiplexer_13_out), .out(multiplexer_19_out), .sel(Opcode_Type));
  Multiplexer #(.width(2), .enable("false")) multiplexer_20 (
    .in0(2'b00), .in1(multiplexer_18_out), .out(multiplexer_20_out), .sel(Opcode_Type));
  assign controlled_buffer_3_out = Opcode_Type ? multiplexer_16_out : 2'bz;  // Controlled_Buffer controlled_buffer_3
  Multiplexer #(.width(2), .enable("false")) multiplexer_21 (
    .in0(multiplexer_20_out), .in1(multiplexer_19_out), .out(multiplexer_21_out), .sel(Sub));
  Multiplexer #(.width(2), .enable("false")) multiplexer_22 (
    .in0(multiplexer_19_out), .in1(multiplexer_20_out), .out(OutBsel), .sel(Sub));
  not not_2 (not_2_out, INC_DEC);
  assign OutCSel = not_2_out ? controlled_buffer_3_out : 2'bz;  // Controlled_Buffer controlled_buffer_4
  not not_3 (not_3_out, ZCNO_Reg[3]);
  not not_4 (not_4_out, INC_DEC);
  assign OutAsel = not_4_out ? multiplexer_21_out : 2'bz;  // Controlled_Buffer controlled_buffer_5
  Adder adder_1 (.a(8'h1), .b(CSAR_q), .out(adder_1_out));  // open: cin, cout
  Decoder #(.select(2), .enable("false")) decoder_2 (.out1(decoder_2_out1), .sel(Branch));  // open: out0, out2, out3
  Multiplexer #(.select(2), .enable("false")) multiplexer_23 (
    .in0(1'b1), .in1(ZCNO_Reg[3]), .in2(ZCNO_Reg[1]), .in3(not_3_out), .out(Condition), .sel(CD));
  and and_2 (and_2_out, decoder_2_out1, Condition);
  assign controlled_buffer_6_out = and_2_out ? adder_1_out : 8'bz;  // Controlled_Buffer controlled_buffer_6
  Multiplexer #(.width(8), .enable("false")) multiplexer_24 (
    .in0(adder_1_out), .in1(Address), .out(multiplexer_24_out), .sel(Condition));
  Register SBR (.D(controlled_buffer_6_out), .Q(SBR_q), .clk(Clock));  // open: en, clr
  Multiplexer #(.enable("false")) multiplexer_25 (
    .in0(IR_8_15[0]), .in1(1'b0), .out(multiplexer_25_out[0]), .sel(Opcode_Type));
  Decoder #(.select(3), .enable("false")) decoder_3 (
    .out1(F1_1), .out2(F1_2), .out3(F1_3), .out4(F1_4), .out5(F1_5), .out6(F1_6), .out7(F1_7), .sel(F1));  // open: out0
  Multiplexer #(.select(2), .width(8), .enable("false")) multiplexer_26 (
    .in0(multiplexer_24_out), .in1(multiplexer_24_out), .in2(SBR_q), .in3(OpcodeMapPlace),
    .out(multiplexer_26_out), .sel(Branch));
  Decoder #(.select(3), .enable("false")) decoder_4 (
    .out1(F2_1), .out2(F2_2), .out3(F2_3), .out4(F2_4), .out5(F2_5), .out6(F2_6), .out7(F2_7), .sel(F2));  // open: out0
  Register CSAR (.D(multiplexer_26_out), .en(1'b1), .Q(CSAR_q), .clk(Clock));  // open: clr
  ROM #(.addrWidth(6)) rom_1 (.addr({IR_8_15[7:3], multiplexer_25_out[0]}), .data(OpcodeMapPlace), .sel(1'b1));
  Multiplexer #(.select(2), .width(2)) multiplexer_27 (
    .in0(2'b00), .in1(2'b00), .in2(2'b01), .in3(2'b10), .out(multiplexer_27_out), .sel(IR_8_15[1:0]),
    .en(IR_8_15[2]));
  assign Address_Regsel = F1_1 ? 3'b001 : 3'bz;  // Controlled_Buffer controlled_buffer_7
  assign Address_Funsel = F1_1 ? 2'b10 : 2'bz;  // Controlled_Buffer controlled_buffer_8
  assign OutDSel = F2_1 ? 2'b00 : 2'bz;  // Controlled_Buffer controlled_buffer_9
  assign IR_LH = F2_1 ? 1'b1 : 1'bz;  // Controlled_Buffer controlled_buffer_10
  assign IR_Enable = F2_1 ? 1'b1 : 1'bz;  // Controlled_Buffer controlled_buffer_11
  assign IR_Funsel = F2_1 ? 2'b11 : 2'bz;  // Controlled_Buffer controlled_buffer_12
  not not_5 (Z_Update, F2_2);
  ROM #(.dataWidth(29)) rom_2 (.addr(multiplexer_26_out), .data(rom_2_data), .sel(1'b1));
  assign Address_Regsel = F1_3 ? 3'b100 : 3'bz;  // Controlled_Buffer controlled_buffer_13
  assign Address_Funsel = F1_3 ? 2'b10 : 2'bz;  // Controlled_Buffer controlled_buffer_14
  assign OutDSel = F2_2 ? 2'b00 : 2'bz;  // Controlled_Buffer controlled_buffer_15
  assign IR_LH = F2_2 ? 1'b0 : 1'bz;  // Controlled_Buffer controlled_buffer_16
  assign IR_Enable = F2_2 ? 1'b1 : 1'bz;  // Controlled_Buffer controlled_buffer_17
  assign IR_Funsel = F2_2 ? 2'b11 : 2'bz;  // Controlled_Buffer controlled_buffer_18
  assign Address_Funsel = F2_3 ? 2'b01 : 2'bz;  // Controlled_Buffer controlled_buffer_19
  assign Register_Funsel = F2_3 ? 2'b01 : 2'bz;  // Controlled_Buffer controlled_buffer_20
  Register #(.width(29)) CSDR (
    .D(rom_2_data), .en(1'b1),
    .Q({ALU_Funsel, MuxAsel, MuxBsel, Regsel_Enable, F1, F2, RAM_Load, RAM_Store, Branch, CD, Address}),
    .clk(Clock));  // open: clr
  and and_3 (and_3_out, F1_2, not_6_out);
  not not_6 (not_6_out, IR_8_15[2]);
  assign OutAsel = and_3_out ? IR_8_15[1:0] : 2'bz;  // Controlled_Buffer controlled_buffer_21
  assign OutCSel = F1_2 ? multiplexer_27_out : 2'bz;  // Controlled_Buffer controlled_buffer_22
  assign Address_Funsel = F2_4 ? 2'b01 : 2'bz;  // Controlled_Buffer controlled_buffer_23
  assign OutCSel = F2_4 ? 2'b11 : 2'bz;  // Controlled_Buffer controlled_buffer_24
  assign OutDSel = F2_4 ? 2'b10 : 2'bz;  // Controlled_Buffer controlled_buffer_25
  assign Address_Funsel = F2_5 ? 2'b01 : 2'bz;  // Controlled_Buffer controlled_buffer_26
  assign Address_Regsel = F2_5 ? 3'b001 : 3'bz;  // Controlled_Buffer controlled_buffer_27
  assign OutDSel = F2_5 ? 2'b10 : 2'bz;  // Controlled_Buffer controlled_buffer_28
  assign OutDSel = F2_6 ? 2'b10 : 2'bz;  // Controlled_Buffer controlled_buffer_29
  assign Register_Funsel = F2_6 ? 2'b01 : 2'bz;  // Controlled_Buffer controlled_buffer_30
  Multiplexer #(.width(2)) multiplexer_28 (
    .in0(2'b10), .in1(2'b11), .out(Register_Funsel), .sel(IR_8_15[3]), .en(F2_7));
  Multiplexer #(.width(2)) multiplexer_29 (.in0(2'b10), .in1(2'b11), .out(Address_Funsel), .sel(IR_8_15[3]), .en(F2_7));
  assign Address_Regsel = F1_4 ? 3'b100 : 3'bz;  // Controlled_Buffer controlled_buffer_31
  assign Address_Funsel = F1_4 ? 2'b11 : 2'bz;  // Controlled_Buffer controlled_buffer_32
  Multiplexer #(.width(3)) multiplexer_30 (
    .in0(3'b000), .in1(3'b001), .out(Address_Regsel), .sel(Condition), .en(F1_5));
  Multiplexer #(.width(2)) multiplexer_31 (.in0(2'b00), .in1(2'b01), .out(Address_Funsel), .sel(Condition), .en(F1_5));
  assign OutDSel = F1_6 ? 2'b01 : 2'bz;  // Controlled_Buffer controlled_buffer_33
  assign OutDSel = F1_7 ? 2'b10 : 2'bz;  // Controlled_Buffer controlled_buffer_34

  // Other names for the same wires on the sheet: Source2[2:0] = IR_0_7[4:2]; Source1[2:0] = IR_0_7[7:5];
  //   D2 = IR_8_15[2]; Dest[2:0] = IR_8_15[2:0]; RAM_Control[1:0] = {RAM_Load, RAM_Store}; D0 = IR_8_15[0];
  //   D1 = IR_8_15[1]; Source2Type = IR_0_7[4]; D3 = IR_8_15[3]; Opcode[4:0] = IR_8_15[7:3]; D4 = IR_8_15[4];
  //   D5 = IR_8_15[5]; D6 = IR_8_15[6]; D7 = IR_8_15[7]; Source1Type = IR_0_7[7]

  // Notes on the sheet:
  //   RegSels
  //   OutSels
  //   Condition
  //   Ram Control
  //   contents of rom_1 (hex, n*v repeats v):
  //   20 24 28 2c 30 34 38 3c 40 44 48 4c 50 54 58 5c 60 64 68 6c 70 74 78 7c 80 84 88 8c 90 94 98 9c a0
  //   a4 a8 ac b0 b4 b8 bc
  //   contents of rom_2 (hex, n*v repeats v):
  //   26001 2ac00 14*0 111011 80012 800 13*0 10c000 0 0 0 9ce000 0 0 0 20c1000 0 0 0 20c1000 0 0 0 1f0c000
  //   0 0 0 1f0c000 0 0 0 e1039 80000 6*0 60041 91a000 6*0 9f0c000 0 0 0 9f0c000 0 0 0 df0c000 0 0 0
  //   df0c000 0 0 0 1f0c059 11c05a 40000 5*0 1f0c061 11c062 40000 5*0 ff0c000 0 0 0 ff0c000 0 0 0 11f0c000
  //   0 0 0 11f0c000 0 0 0 5f0c000 0 0 0 5f0c000 0 0 0 15f0c000 0 0 0 15f0c000 0 0 0 17f0c000 0 0 0
  //   17f0c000 0 0 0 2a0000 7*0 2a0100 7*0 2a0300 7*0 410 2a0000 6*0 600b1 416000
  //   F1 - F2
endmodule
