// Logisim project OverflowChecker.circ as structural Verilog: 1 circuit, main circuit main
module main (
  input  [7:0] Output,
  input  [7:0] A,
  input  [7:0] B,
  input  [3:0] Funsel,
  output OverflowOut
);

  wire A_B_2_out, A_B_Carry_out, A_B_out, neg_neg_pos_out, neg_pos_pos_out, not_1_out, not_2_out, not_3_out,
       not_4_out, not_5_out, not_6_out, not_7_out, not_8_out, not_9_out, not_10_out, not_11_out, not_12_out,
       not_13_out, or_1_out, pos_neg_neg_out, pos_pos_neg_out;

  not not_1 (not_1_out, Funsel[0]);
  not not_2 (not_2_out, Funsel[1]);
  not not_3 (not_3_out, Funsel[3]);
  not not_4 (not_4_out, Funsel[1]);
  not not_5 (not_5_out, Funsel[3]);
  not not_6 (not_6_out, Funsel[0]);
  not not_7 (not_7_out, Funsel[3]);
  and A_B (A_B_out, not_1_out, not_2_out, Funsel[2], not_3_out);
  and A_B_Carry (A_B_Carry_out, Funsel[0], not_4_out, Funsel[2], not_5_out);
  and A_B_2 (A_B_2_out, not_6_out, Funsel[1], Funsel[2], not_7_out);
  or or_1 (or_1_out, A_B_out, A_B_Carry_out);
  not not_8 (not_8_out, A[7]);
  not not_9 (not_9_out, B[7]);
  not not_10 (not_10_out, Output[7]);
  not not_11 (not_11_out, A[7]);
  not not_12 (not_12_out, Output[7]);
  not not_13 (not_13_out, B[7]);
  and pos_pos_neg (pos_pos_neg_out, Output[7], not_8_out, not_9_out, or_1_out);
  and neg_neg_pos (neg_neg_pos_out, not_10_out, A[7], B[7], or_1_out);
  and pos_neg_neg (pos_neg_neg_out, Output[7], not_11_out, B[7], A_B_2_out);
  and neg_pos_pos (neg_pos_pos_out, not_12_out, A[7], not_13_out, A_B_2_out);
  or u_OverflowOut (OverflowOut, pos_pos_neg_out, neg_neg_pos_out, pos_neg_neg_out, neg_pos_pos_out);
endmodule
