// Logisim project Registers.circ as structural Verilog: 2 circuits, main circuit 16-bit register
module _16_bit_register (
  input  Enable,
  input  Clear,
  input  Clock,
  input  [15:0] I,
  output [15:0] Q
);

  Hex_Digit_Display hex_digit_display_1 (.value(I[15:12]));  // open: dp
  Hex_Digit_Display hex_digit_display_2 (.value(I[11:8]));  // open: dp
  Hex_Digit_Display hex_digit_display_3 (.value(I[7:4]));  // open: dp
  Hex_Digit_Display hex_digit_display_4 (.value(I[3:0]));  // open: dp
  _8_bit_register u_8_bit_register_1 (.I(I[7:0]), .Enable(Enable), .Clear(Clear), .Clock(Clock), .Q(Q[7:0]));
  _8_bit_register u_8_bit_register_2 (.I(I[15:8]), .Enable(Enable), .Clear(Clear), .Clock(Clock), .Q(Q[15:8]));
  Hex_Digit_Display hex_digit_display_5 (.value(Q[15:12]));  // open: dp
  Hex_Digit_Display hex_digit_display_6 (.value(Q[11:8]));  // open: dp
  Hex_Digit_Display hex_digit_display_7 (.value(Q[3:0]));  // open: dp
  Hex_Digit_Display hex_digit_display_8 (.value(Q[7:4]));  // open: dp
endmodule

// 8-bit R
module _8_bit_register (
  input  Enable,
  input  Clear,
  input  Clock,
  input  [7:0] I,
  output [7:0] Q
);

  Hex_Digit_Display hex_digit_display_1 (.value(I[7:4]));  // open: dp
  Hex_Digit_Display hex_digit_display_2 (.value(I[3:0]));  // open: dp
  D_Flip_Flop d_ff_1 (.clk(Clock), .D(I[0]), .Q(Q[0]), .en(Enable), .reset(Clear));  // open: Qn, preset
  D_Flip_Flop d_ff_2 (.clk(Clock), .D(I[1]), .Q(Q[1]), .en(Enable), .reset(Clear));  // open: Qn, preset
  D_Flip_Flop d_ff_3 (.clk(Clock), .D(I[2]), .Q(Q[2]), .en(Enable), .reset(Clear));  // open: Qn, preset
  D_Flip_Flop d_ff_4 (.clk(Clock), .D(I[3]), .Q(Q[3]), .en(Enable), .reset(Clear));  // open: Qn, preset
  D_Flip_Flop d_ff_5 (.clk(Clock), .D(I[4]), .Q(Q[4]), .en(Enable), .reset(Clear));  // open: Qn, preset
  D_Flip_Flop d_ff_6 (.clk(Clock), .D(I[5]), .Q(Q[5]), .en(Enable), .reset(Clear));  // open: Qn, preset
  D_Flip_Flop d_ff_7 (.clk(Clock), .D(I[6]), .Q(Q[6]), .en(Enable), .reset(Clear));  // open: Qn, preset
  D_Flip_Flop d_ff_8 (.clk(Clock), .D(I[7]), .Q(Q[7]), .en(Enable), .reset(Clear));  // open: Qn, preset
  Hex_Digit_Display hex_digit_display_3 (.value(Q[7:4]));  // open: dp
  Hex_Digit_Display hex_digit_display_4 (.value(Q[3:0]));  // open: dp
endmodule
