// Logisim project Project-1-Group-29.circ as structural Verilog: 5 circuits, main circuit Part-1
module Part_1 (
  input  [7:0] I,
  input  Clock,
  input  [1:0] FunSel,
  input  E,
  output [7:0] Q
);

  wire [7:0] adder_1_out, multiplexer_1_out, subtractor_1_out;

  Multiplexer #(.select(2), .width(8)) multiplexer_1 (
    .in0({8{1'b0}}), .in1(I), .in2(adder_1_out), .in3(subtractor_1_out), .out(multiplexer_1_out),
    .sel(FunSel), .en(E));
  _8_bit_register u_8_bit_register_1 (.I(multiplexer_1_out), .Clock(Clock), .Q(Q));  // open: Enable, Clear
  Hex_Digit_Display hex_digit_display_1 (.value(I[3:0]));  // open: dp
  Hex_Digit_Display hex_digit_display_2 (.value(I[7:4]));  // open: dp
  Hex_Digit_Display hex_digit_display_3 (.value(Q[3:0]));  // open: dp
  Hex_Digit_Display hex_digit_display_4 (.value(Q[7:4]));  // open: dp
  Adder adder_1 (.a(Q), .b(8'h1), .out(adder_1_out));  // open: cin, cout
  Subtractor subtractor_1 (.a(Q), .b(8'h1), .out(subtractor_1_out));  // open: bin, bout
endmodule

module Part_2c (
  input  [7:0] Input,
  input  Low_High,
  input  Enable,
  input  [1:0] FunSel,
  output [15:0] IRout
);

  wire Clock_out;
  wire [15:0] adder_1_out, multiplexer_1_out, multiplexer_2_out, subtractor_1_out;

  Hex_Digit_Display hex_digit_display_1 (.value(Input[7:4]));  // open: dp
  Hex_Digit_Display hex_digit_display_2 (.value(Input[3:0]));  // open: dp
  Multiplexer #(.select(2), .width(16), .enable("false")) multiplexer_1 (
    .in0({16{1'b0}}), .in1(adder_1_out), .in2(subtractor_1_out), .in3(multiplexer_2_out),
    .out(multiplexer_1_out), .sel(FunSel));
  Multiplexer #(.width(16), .enable("false")) multiplexer_2 (
    .in0({IRout[15:8], Input}), .in1({Input, IRout[7:0]}), .out(multiplexer_2_out), .sel(Low_High));
  Clock Clock (.out(Clock_out));
  _8_bit_register IR_0_7 (
    .I(multiplexer_1_out[7:0]), .Enable(Enable), .Clock(Clock_out), .Q(IRout[7:0]));  // open: Clear
  _8_bit_register IR_8_15 (
    .I(multiplexer_1_out[15:8]), .Enable(Enable), .Clock(Clock_out), .Q(IRout[15:8]));  // open: Clear
  Adder #(.width(16)) adder_1 (.a(IRout), .b(16'h1), .out(adder_1_out));  // open: cin, cout
  Subtractor #(.width(16)) subtractor_1 (.a(IRout), .b(16'h1), .out(subtractor_1_out));  // open: bin, bout
  Hex_Digit_Display hex_digit_display_3 (.value(IRout[15:12]));  // open: dp
  Hex_Digit_Display hex_digit_display_4 (.value(IRout[11:8]));  // open: dp
  Hex_Digit_Display hex_digit_display_5 (.value(IRout[7:4]));  // open: dp
  Hex_Digit_Display hex_digit_display_6 (.value(IRout[3:0]));  // open: dp
endmodule

module Part_2a (
  input  [7:0] \input ,
  input  [1:0] OutASel,
  input  [1:0] OutBSel,
  input  [1:0] FunSel,
  input  [3:0] RegSel,
  output [7:0] OutA,
  output [7:0] OutB
);

  wire Clock_out;
  wire [7:0] R0_q, R1_q, R2_q, R3_q;

  Hex_Digit_Display hex_digit_display_1 (.value(\input [3:0]));  // open: dp
  Hex_Digit_Display hex_digit_display_2 (.value(\input [7:4]));  // open: dp
  Clock Clock (.out(Clock_out));
  Part_1 R0 (.I(\input ), .Clock(Clock_out), .FunSel(FunSel), .E(RegSel[0]), .Q(R0_q));
  Part_1 R1 (.I(\input ), .Clock(Clock_out), .FunSel(FunSel), .E(RegSel[1]), .Q(R1_q));
  Part_1 R2 (.I(\input ), .Clock(Clock_out), .FunSel(FunSel), .E(RegSel[2]), .Q(R2_q));
  Part_1 R3 (.I(\input ), .Clock(Clock_out), .FunSel(FunSel), .E(RegSel[3]), .Q(R3_q));
  Multiplexer #(.select(2), .width(8), .enable("false")) multiplexer_1 (
    .in0(R0_q), .in1(R1_q), .in2(R2_q), .in3(R3_q), .out(OutA), .sel(OutASel));
  Multiplexer #(.select(2), .width(8), .enable("false")) multiplexer_2 (
    .in0(R0_q), .in1(R1_q), .in2(R2_q), .in3(R3_q), .out(OutB), .sel(OutBSel));
  Hex_Digit_Display hex_digit_display_3 (.value(OutA[3:0]));  // open: dp
  Hex_Digit_Display hex_digit_display_4 (.value(OutA[7:4]));  // open: dp
  Hex_Digit_Display hex_digit_display_5 (.value(OutB[3:0]));  // open: dp
  Hex_Digit_Display hex_digit_display_6 (.value(OutB[7:4]));  // open: dp
endmodule

module Part_2b (
  input  [7:0] \input ,
  input  [1:0] OutCSel,
  input  [1:0] OutDSel,
  input  [1:0] FunSel,
  input  [2:0] RegSel,
  output [7:0] OutC,
  output [7:0] OutD
);

  wire Clock_out;
  wire [7:0] AR_q, PC_q, SP_q;

  Hex_Digit_Display hex_digit_display_1 (.value(\input [7:4]));  // open: dp
  Hex_Digit_Display hex_digit_display_2 (.value(\input [3:0]));  // open: dp
  Part_1 PC (.I(\input ), .Clock(Clock_out), .FunSel(FunSel), .E(RegSel[0]), .Q(PC_q));
  Part_1 AR (.I(\input ), .Clock(Clock_out), .FunSel(FunSel), .E(RegSel[1]), .Q(AR_q));
  Part_1 SP (.I(\input ), .Clock(Clock_out), .FunSel(FunSel), .E(RegSel[2]), .Q(SP_q));
  Clock Clock (.out(Clock_out));
  Multiplexer #(.select(2), .width(8), .enable("false")) multiplexer_1 (
    .in0(PC_q), .in1(AR_q), .in2(SP_q), .in3(PC_q), .out(OutC), .sel(OutCSel));
  Multiplexer #(.select(2), .width(8), .enable("false")) multiplexer_2 (
    .in0(PC_q), .in1(AR_q), .in2(SP_q), .in3(PC_q), .out(OutD), .sel(OutDSel));
  Hex_Digit_Display hex_digit_display_3 (.value(OutC[7:4]));  // open: dp
  Hex_Digit_Display hex_digit_display_4 (.value(OutC[3:0]));  // open: dp
  Hex_Digit_Display hex_digit_display_5 (.value(OutD[7:4]));  // open: dp
  Hex_Digit_Display hex_digit_display_6 (.value(OutD[3:0]));  // open: dp
endmodule

module Part_1_Simulation (
  input  [7:0] I,
  input  Enable,
  input  [1:0] FunSel,
  output [7:0] Q
);

  wire Clock_out;

  Part_1 Part_1 (.I(I), .Clock(Clock_out), .FunSel(FunSel), .E(Enable), .Q(Q));
  Hex_Digit_Display hex_digit_display_1 (.value(I[3:0]));  // open: dp
  Hex_Digit_Display hex_digit_display_2 (.value(I[7:4]));  // open: dp
  Hex_Digit_Display hex_digit_display_3 (.value(Q[7:4]));  // open: dp
  Clock Clock (.out(Clock_out));
  Hex_Digit_Display hex_digit_display_4 (.value(Q[3:0]));  // open: dp
endmodule
