// Logisim project Main Circuit.circ as structural Verilog: 2 circuits, main circuit part-1
// ALU
module part_1 (
  input  Clock,
  input  [7:0] A,
  input  [7:0] B,
  input  Clear,
  input  [3:0] FunSel,
  output [7:0] OutALU,
  output [3:0] ZCNO
);

  wire adder_1_cout, adder_2_cout, adder_3_cout, and_2_out, main_1_carry_out, main_2_overflow,
       main_3_carry_out, main_3_overflow, multiplexer_1_out, multiplexer_2_out, multiplexer_4_out, not_4_out,
       not_5_out, Overflow_Checker_2_overflowout, Overflow_Checker_3_overflowout,
       Overflow_Checker_overflowout, Zero_Output_Checker_out;
  wire [7:0] adder_1_out, adder_2_out, adder_3_out, and_1_out, main_1_output, main_2_output, main_3_output,
       not_1_out, not_2_out, not_3_out, or_1_out, xor_1_out;

  Hex_Digit_Display hex_digit_display_1 (.value(A[3:0]));  // open: dp
  Hex_Digit_Display hex_digit_display_2 (.value(A[7:4]));  // open: dp
  Hex_Digit_Display hex_digit_display_3 (.value(B[7:4]));  // open: dp
  Hex_Digit_Display hex_digit_display_4 (.value(B[3:0]));  // open: dp
  assign not_1_out = ~B;  // NOT_Gate not_1, 8 bits wide
  assign not_2_out = ~A;  // NOT_Gate not_2, 8 bits wide
  assign not_3_out = ~B;  // NOT_Gate not_3, 8 bits wide
  Adder adder_1 (.a(A), .b(B), .out(adder_1_out), .cin(1'b0), .cout(adder_1_cout));
  Adder adder_2 (.a(A), .b(B), .out(adder_2_out), .cin(ZCNO[2]), .cout(adder_2_cout));
  Adder adder_3 (.a(A), .b(not_1_out), .out(adder_3_out), .cin(1'b1), .cout(adder_3_cout));
  assign and_1_out = A & B;  // AND_Gate and_1, 8 bits wide
  assign or_1_out = A | B;  // OR_Gate or_1, 8 bits wide
  assign xor_1_out = A ^ B;  // XOR_Gate xor_1, 8 bits wide
  Logical_Shift_main main_1 (.Input(A), .Left_Right(FunSel[0]), .Carry_Out(main_1_carry_out), .Output(main_1_output));
  Arithmetic_Shift_main main_2 (.Input(A), .Left_Right(FunSel[0]), .Output(main_2_output), .Overflow(main_2_overflow));
  circular_shift_main main_3 (
    .Input(A), .Carry_In(ZCNO[2]), .Left_Right(FunSel[0]), .Carry_Out(main_3_carry_out),
    .Output(main_3_output), .Overflow(main_3_overflow));
  OverflowChecker_main Overflow_Checker (
    .Funsel(FunSel), .OverflowOut(Overflow_Checker_overflowout), .Output(adder_1_out), .A(A), .B(B));
  OverflowChecker_main Overflow_Checker_2 (
    .Funsel(FunSel), .OverflowOut(Overflow_Checker_2_overflowout), .Output(adder_2_out), .A(A), .B(A));
  OverflowChecker_main Overflow_Checker_3 (
    .Funsel(FunSel), .OverflowOut(Overflow_Checker_3_overflowout), .Output(adder_3_out), .A(A), .B(B));
  Multiplexer #(.select(4), .enable("false")) multiplexer_1 (
    .in0(ZCNO[2]), .in1(ZCNO[2]), .in2(ZCNO[2]), .in3(ZCNO[2]), .in4(adder_1_cout), .in5(adder_2_cout),
    .in6(adder_3_cout), .in7(ZCNO[2]), .in8(ZCNO[2]), .in9(ZCNO[2]), .in10(main_1_carry_out),
    .in11(main_1_carry_out), .in12(ZCNO[2]), .in13(ZCNO[2]), .in14(main_3_carry_out),
    .in15(main_3_carry_out), .out(multiplexer_1_out), .sel(FunSel));
  Multiplexer #(.select(4), .enable("false")) multiplexer_2 (
    .in0(ZCNO[0]), .in1(ZCNO[0]), .in2(ZCNO[0]), .in3(ZCNO[0]), .in4(Overflow_Checker_overflowout),
    .in5(Overflow_Checker_2_overflowout), .in6(Overflow_Checker_3_overflowout), .in7(ZCNO[0]), .in8(ZCNO[0]),
    .in9(ZCNO[0]), .in10(ZCNO[0]), .in11(ZCNO[0]), .in12(main_2_overflow), .in13(ZCNO[0]),
    .in14(main_3_overflow), .in15(main_3_overflow), .out(multiplexer_2_out), .sel(FunSel));
  Multiplexer #(.select(4), .width(8), .enable("false")) multiplexer_3 (
    .in0(A), .in1(B), .in2(not_2_out), .in3(not_3_out), .in4(adder_1_out), .in5(adder_2_out),
    .in6(adder_3_out), .in7(and_1_out), .in8(or_1_out), .in9(xor_1_out), .in10(main_1_output),
    .in11(main_1_output), .in12(main_2_output), .in13(main_2_output), .in14(main_3_output),
    .in15(main_3_output), .out(OutALU), .sel(FunSel));
  not not_4 (not_4_out, Zero_Output_Checker_out);
  D_Flip_Flop Z (.clk(Clock), .D(not_4_out), .Q(ZCNO[3]), .en(1'b1), .reset(Clear));  // open: Qn, preset
  or Zero_Output_Checker (Zero_Output_Checker_out, OutALU[0], OutALU[1], OutALU[2], OutALU[3], OutALU[4], OutALU[5], OutALU[6], OutALU[7]);
  D_Flip_Flop C (.clk(Clock), .D(multiplexer_1_out), .Q(ZCNO[2]), .en(1'b1), .reset(Clear));  // open: Qn, preset
  Hex_Digit_Display hex_digit_display_5 (.value(OutALU[7:4]));  // open: dp
  D_Flip_Flop N (.clk(Clock), .D(multiplexer_4_out), .Q(ZCNO[1]), .en(1'b1), .reset(Clear));  // open: Qn, preset
  Hex_Digit_Display hex_digit_display_6 (.value(OutALU[3:0]));  // open: dp
  D_Flip_Flop O (.clk(Clock), .D(multiplexer_2_out), .Q(ZCNO[0]), .en(1'b1), .reset(Clear));  // open: Qn, preset
  not not_5 (not_5_out, FunSel[1]);
  and and_2 (and_2_out, FunSel[3], FunSel[2], not_5_out, FunSel[0]);
  Multiplexer #(.enable("false")) multiplexer_4 (
    .in0(OutALU[7]), .in1(ZCNO[1]), .out(multiplexer_4_out), .sel(and_2_out));

  // Notes on the sheet:
  //   A
  //   B
  //   Logical Shift
  //   Arithmetic Shift
  //   Circular Shift
endmodule

module part_2 (
  input  MuxCSel,
  input  [1:0] OutASel,
  input  [3:0] FunSel,
  input  Clear,
  input  [1:0] OutBSel,
  input  [3:0] RegSel,
  input  [1:0] FunSel_2,
  input  [1:0] MuxASel,
  input  [1:0] OutCSel,
  input  [1:0] MuxBSel,
  input  in_11,
  input  in_12,
  input  [1:0] OutDSel,
  input  [2:0] RegSel_2,
  input  [1:0] FunSel_3,
  input  [1:0] FunSel_4,
  input  Enable,
  input  L_H,
  output [3:0] ZCNO,
  output [7:0] IR_8_15
);

  wire Clock_out;
  wire [7:0] Address_Register_File_outc, Address_Register_File_outd, IR_irout, multiplexer_1_out,
       multiplexer_2_out, multiplexer_3_out, part_1_1_outalu, ram_1_data, Register_File_outa,
       Register_File_outb;

  Multiplexer #(.select(2), .width(8), .enable("false")) multiplexer_1 (
    .in0(IR_irout), .in1(ram_1_data), .in2(Address_Register_File_outc), .in3(part_1_1_outalu),
    .out(multiplexer_1_out), .sel(MuxASel));
  Part_2a Register_File (
    .\input (multiplexer_1_out), .Clock(Clock_out), .OutASel(OutASel), .OutBSel(OutBSel), .RegSel(RegSel),
    .FunSel(FunSel_2), .OutA(Register_File_outa), .OutB(Register_File_outb));
  Part_2c IR (
    .Input(ram_1_data), .Low_High(L_H), .Enable(Enable), .IRout({IR_8_15, IR_irout}), .FunSel(FunSel_4),
    .Clock(Clock_out));
  Multiplexer #(.select(2), .width(8), .enable("false")) multiplexer_2 (
    .in1(IR_irout), .in2(ram_1_data), .in3(part_1_1_outalu), .out(multiplexer_2_out), .sel(MuxBSel));  // open: in0
  Multiplexer #(.width(8), .enable("false")) multiplexer_3 (
    .in0(multiplexer_1_out), .in1(Register_File_outa), .out(multiplexer_3_out), .sel(MuxCSel));
  Part_2b Address_Register_File (
    .\input (multiplexer_2_out), .Clock(Clock_out), .OutCSel(OutCSel), .OutDSel(OutDSel), .RegSel(RegSel_2),
    .FunSel(FunSel_3), .OutC(Address_Register_File_outc), .OutD(Address_Register_File_outd));
  Hex_Digit_Display hex_digit_display_1 (.value(IR_8_15[7:4]));  // open: dp
  Clock Clock (.out(Clock_out));
  part_1 part_1_1 (
    .Clock(Clock_out), .A(multiplexer_3_out), .B(Register_File_outb), .ZCNO(ZCNO), .FunSel(FunSel),
    .Clear(Clear), .OutALU(part_1_1_outalu));
  Hex_Digit_Display hex_digit_display_2 (.value(IR_8_15[3:0]));  // open: dp
  RAM #(.bus("separate")) ram_1 (
    .addr(Address_Register_File_outd), .din(part_1_1_outalu), .data(ram_1_data), .str(in_11),
    .clk(Clock_out), .ld(in_12));  // open: sel, clr
endmodule
