// Logisim project Main Circuit.circ as structural Verilog: 6 circuits, main circuit part-1
// ALU
module part_1 (
  input  Clock,
  input  [7:0] A,
  input  [7:0] B,
  input  Clear,
  input  [3:0] FunSel,
  output [7:0] OutALU,
  output [3:0] ZCNO
);

  wire adder_1_cout, adder_2_cout, adder_3_cout, and_2_out, main_1_carry_out, main_2_overflow,
       main_3_carry_out, main_3_overflow, multiplexer_1_out, multiplexer_2_out, multiplexer_4_out, not_4_out,
       not_5_out, Overflow_Checker_2_overflowout, Overflow_Checker_3_overflowout,
       Overflow_Checker_overflowout, Zero_Output_Checker_out;
  wire [7:0] adder_1_out, adder_2_out, adder_3_out, and_1_out, main_1_output, main_2_output, main_3_output,
       not_1_out, not_2_out, not_3_out, or_1_out, xor_1_out;

  Hex_Digit_Display hex_digit_display_1 (.value(A[7:4]));  // open: dp
  Hex_Digit_Display hex_digit_display_2 (.value(A[3:0]));  // open: dp
  Hex_Digit_Display hex_digit_display_3 (.value(B[3:0]));  // open: dp
  Hex_Digit_Display hex_digit_display_4 (.value(B[7:4]));  // open: dp
  assign not_1_out = ~B;  // NOT_Gate not_1, 8 bits wide
  assign not_2_out = ~A;  // NOT_Gate not_2, 8 bits wide
  assign not_3_out = ~B;  // NOT_Gate not_3, 8 bits wide
  Adder adder_1 (.a(A), .b(B), .out(adder_1_out), .cin(1'b0), .cout(adder_1_cout));
  Adder adder_2 (.a(A), .b(B), .out(adder_2_out), .cin(ZCNO[2]), .cout(adder_2_cout));
  Adder adder_3 (.a(A), .b(not_1_out), .out(adder_3_out), .cin(1'b1), .cout(adder_3_cout));
  assign and_1_out = A & B;  // AND_Gate and_1, 8 bits wide
  assign or_1_out = A | B;  // OR_Gate or_1, 8 bits wide
  assign xor_1_out = A ^ B;  // XOR_Gate xor_1, 8 bits wide
  Logical_Shift_main main_1 (.Input(A), .Left_Right(FunSel[0]), .Carry_Out(main_1_carry_out), .Output(main_1_output));
  Arithmetic_Shift_main main_2 (.Input(A), .Left_Right(FunSel[0]), .Output(main_2_output), .Overflow(main_2_overflow));
  circular_shift_main main_3 (
    .Input(A), .Carry_In(ZCNO[2]), .Left_Right(FunSel[0]), .Carry_Out(main_3_carry_out),
    .Output(main_3_output), .Overflow(main_3_overflow));
  OverflowChecker_main Overflow_Checker (
    .Funsel(FunSel), .OverflowOut(Overflow_Checker_overflowout), .Output(adder_1_out), .A(A), .B(B));
  OverflowChecker_main Overflow_Checker_2 (
    .Funsel(FunSel), .OverflowOut(Overflow_Checker_2_overflowout), .Output(adder_2_out), .A(A), .B(A));
  OverflowChecker_main Overflow_Checker_3 (
    .Funsel(FunSel), .OverflowOut(Overflow_Checker_3_overflowout), .Output(adder_3_out), .A(A), .B(B));
  Multiplexer #(.select(4), .enable("false")) multiplexer_1 (
    .in0(ZCNO[2]), .in1(ZCNO[2]), .in2(ZCNO[2]), .in3(ZCNO[2]), .in4(adder_1_cout), .in5(adder_2_cout),
    .in6(adder_3_cout), .in7(ZCNO[2]), .in8(ZCNO[2]), .in9(ZCNO[2]), .in10(main_1_carry_out),
    .in11(main_1_carry_out), .in12(ZCNO[2]), .in13(ZCNO[2]), .in14(main_3_carry_out),
    .in15(main_3_carry_out), .out(multiplexer_1_out), .sel(FunSel));
  Multiplexer #(.select(4), .enable("false")) multiplexer_2 (
    .in0(ZCNO[0]), .in1(ZCNO[0]), .in2(ZCNO[0]), .in3(ZCNO[0]), .in4(Overflow_Checker_overflowout),
    .in5(Overflow_Checker_2_overflowout), .in6(Overflow_Checker_3_overflowout), .in7(ZCNO[0]), .in8(ZCNO[0]),
    .in9(ZCNO[0]), .in10(ZCNO[0]), .in11(ZCNO[0]), .in12(main_2_overflow), .in13(ZCNO[0]),
    .in14(main_3_overflow), .in15(main_3_overflow), .out(multiplexer_2_out), .sel(FunSel));
  Multiplexer #(.select(4), .width(8), .enable("false")) multiplexer_3 (
    .in0(A), .in1(B), .in2(not_2_out), .in3(not_3_out), .in4(adder_1_out), .in5(adder_2_out),
    .in6(adder_3_out), .in7(and_1_out), .in8(or_1_out), .in9(xor_1_out), .in10(main_1_output),
    .in11(main_1_output), .in12(main_2_output), .in13(main_2_output), .in14(main_3_output),
    .in15(main_3_output), .out(OutALU), .sel(FunSel));
  not not_4 (not_4_out, Zero_Output_Checker_out);
  D_Flip_Flop Z (.clk(Clock), .D(not_4_out), .Q(ZCNO[3]), .en(1'b1), .reset(Clear));  // open: Qn, preset
  or Zero_Output_Checker (Zero_Output_Checker_out, OutALU[0], OutALU[1], OutALU[2], OutALU[3], OutALU[4], OutALU[5], OutALU[6], OutALU[7]);
  D_Flip_Flop C (.clk(Clock), .D(multiplexer_1_out), .Q(ZCNO[2]), .en(1'b1), .reset(Clear));  // open: Qn, preset
  Hex_Digit_Display hex_digit_display_5 (.value(OutALU[7:4]));  // open: dp
  D_Flip_Flop N (.clk(Clock), .D(multiplexer_4_out), .Q(ZCNO[1]), .en(1'b1), .reset(Clear));  // open: Qn, preset
  Hex_Digit_Display hex_digit_display_6 (.value(OutALU[3:0]));  // open: dp
  D_Flip_Flop O (.clk(Clock), .D(multiplexer_2_out), .Q(ZCNO[0]), .en(1'b1), .reset(Clear));  // open: Qn, preset
  not not_5 (not_5_out, FunSel[1]);
  and and_2 (and_2_out, FunSel[3], FunSel[2], not_5_out, FunSel[0]);
  Multiplexer #(.enable("false")) multiplexer_4 (
    .in0(OutALU[7]), .in1(ZCNO[1]), .out(multiplexer_4_out), .sel(and_2_out));

  // Notes on the sheet:
  //   A
  //   B
  //   Logical Shift
  //   Arithmetic Shift
  //   Circular Shift
endmodule

module part_2 (
  input  Clear,
  output [3:0] out_2,
  output [1:0] out_3,
  output [2:0] out_4,
  output [7:0] IR_8_15,
  output [7:0] IR_0_7
);

  wire Clock_out, INC_DEC, IR_Enable, IR_LH, MuxCSel, RAM_Load, RAM_Store, Register_ALU;
  wire [1:0] Address_Funsel, IR_Funsel, MuxASel, MuxBSel, OutAsel, OutBsel, OutCsel, OutDsel;
  wire [2:0] Address_Regsel;
  wire [3:0] ALU_Funsel, ZCNO;
  wire [7:0] Address_Register_File_outc, Address_Register_File_outd, multiplexer_1_out, multiplexer_2_out,
       multiplexer_3_out, multiplexer_4_out, multiplexer_5_out, n8_bit_register_1_q, part_1_1_outalu,
       ram_1_data, Register_File_outa, Register_File_outb;

  Multiplexer #(.select(2), .width(8), .enable("false")) multiplexer_1 (
    .in0(IR_0_7), .in1(ram_1_data), .in2(Address_Register_File_outc), .in3(multiplexer_5_out),
    .out(multiplexer_1_out), .sel(MuxASel));
  Part_2a Register_File (
    .\input (multiplexer_1_out), .Clock(Clock_out), .OutASel(OutAsel), .OutBSel(OutBsel), .RegSel(out_2),
    .FunSel(out_3), .OutA(Register_File_outa), .OutB(Register_File_outb));
  Part_2c IR (
    .Input(ram_1_data), .Low_High(IR_LH), .Enable(IR_Enable), .IRout({IR_8_15, IR_0_7}), .FunSel(IR_Funsel),
    .Clock(Clock_out));
  Multiplexer #(.select(2), .width(8), .enable("false")) multiplexer_2 (
    .in1(IR_0_7), .in2(ram_1_data), .in3(multiplexer_5_out), .out(multiplexer_2_out), .sel(MuxBSel));  // open: in0
  Multiplexer #(.width(8), .enable("false")) multiplexer_3 (
    .in0(multiplexer_1_out), .in1(Register_File_outa), .out(multiplexer_3_out), .sel(MuxCSel));
  Multiplexer #(.width(8), .enable("false")) multiplexer_4 (
    .in0(Register_File_outb), .in1(8'h1), .out(multiplexer_4_out), .sel(INC_DEC));
  Part_2b Address_Register_File (
    .\input (multiplexer_2_out), .Clock(Clock_out), .OutCSel(OutCsel), .OutDSel(OutDsel),
    .RegSel(Address_Regsel), .FunSel(Address_Funsel), .OutC(Address_Register_File_outc),
    .OutD(Address_Register_File_outd));
  Hex_Digit_Display hex_digit_display_1 (.value(IR_8_15[7:4]));  // open: dp
  Clock Clock (.out(Clock_out));
  part_1 part_1_1 (
    .Clock(Clock_out), .A(multiplexer_3_out), .B(multiplexer_4_out), .ZCNO(ZCNO), .FunSel(ALU_Funsel),
    .Clear(Clear), .OutALU(part_1_1_outalu));
  Hex_Digit_Display hex_digit_display_2 (.value(IR_8_15[3:0]));  // open: dp
  _8_bit_register u_8_bit_register_1 (
    .I(part_1_1_outalu), .Clock(Clock_out), .Q(n8_bit_register_1_q));  // open: Enable, Clear
  Multiplexer #(.width(8), .enable("false")) multiplexer_5 (
    .in0(part_1_1_outalu), .in1(n8_bit_register_1_q), .out(multiplexer_5_out), .sel(Register_ALU));
  RAM #(.bus("separate")) ram_1 (
    .addr(Address_Register_File_outd), .din(multiplexer_5_out), .data(ram_1_data), .str(RAM_Store),
    .clk(Clock_out), .ld(RAM_Load));  // open: sel, clr
  control_unit Control_Unit (
    .Address_Regsel(Address_Regsel), .Address_Funsel(Address_Funsel), .Register_Regsel(out_2),
    .Register_Funsel(out_3), .RAM_Store(RAM_Store), .RAM_Load(RAM_Load), .MuxAsel(MuxASel),
    .MuxBsel(MuxBSel), .MuxCSel(MuxCSel), .OutDSel(OutDsel), .out_22(out_4), .Clock(Clock_out),
    .IR_Funsel(IR_Funsel), .IR_Enable(IR_Enable), .IR_LH(IR_LH), .IR_8_15(IR_8_15), .IR_0_7(IR_0_7),
    .ALU_Funsel(ALU_Funsel), .ZCNO(ZCNO), .OutAsel(OutAsel), .OutBsel(OutBsel), .OutCSel(OutCsel),
    .INC_DEC(INC_DEC), .Register_ALU(Register_ALU));

  // Other names for the same wires on the sheet: Register_Funsel[1:0] = out_3; Register_Regsel[3:0] = out_2
endmodule

module control_unit (
  input  [7:0] IR_8_15,
  input  [7:0] IR_0_7,
  input  Clock,
  input  [3:0] ZCNO,
  output [1:0] IR_Funsel,
  output [2:0] Address_Regsel,
  output IR_Enable,
  output [1:0] Address_Funsel,
  output IR_LH,
  output [3:0] Register_Regsel,
  output [1:0] Register_Funsel,
  output RAM_Store,
  output [3:0] ALU_Funsel,
  output RAM_Load,
  output [1:0] MuxAsel,
  output [1:0] OutAsel,
  output [1:0] MuxBsel,
  output [1:0] OutBsel,
  output MuxCSel,
  output [1:0] OutCSel,
  output [1:0] OutDSel,
  output [2:0] out_22,
  output INC_DEC,
  output Register_ALU
);

  wire Clear, EN_00, EN_0E, EN_0F, EN_01, EN_02_0B_0C_0D, EN_03, EN_04, EN_05, EN_06, EN_07_08, EN_09_0A,
       EN_10, EN_11, EN_12, OP_00, OP_0A, OP_0B, OP_0C, OP_0D, OP_0E, OP_0F, OP_01, OP_02, OP_02_0B_0C_0D,
       OP_03, OP_04, OP_05, OP_06, OP_07, OP_07_08, OP_08, OP_09, OP_09_0A, OP_10, OP_11, OP_12, or_1_out,
       T0, T1, T2, T2_T5, T3, T4, T5, T6, T7;
  wire [1:0] OutASel_t, OutCSel_t, register_1_q, register_2_q, register_3_q;

  Counter #(.width(3), .max('h7)) counter_1 (
    .count(Clock), .Q(out_22), .clk(Clock), .clr(Clear));  // open: load, D, carry
  Decoder #(.select(3), .disabled(0), .enable("false")) decoder_1 (
    .out0(T0), .out1(T1), .out2(T2), .out3(T3), .out4(T4), .out5(T5), .out6(T6), .out7(T7), .sel(out_22));
  Decoder #(.select(5), .disabled(0), .enable("false")) decoder_2 (
    .out0(OP_00), .out1(OP_01), .out2(OP_02), .out3(OP_03), .out4(OP_04), .out5(OP_05), .out6(OP_06),
    .out7(OP_07), .out8(OP_08), .out9(OP_09), .out10(OP_0A), .out11(OP_0B), .out12(OP_0C), .out13(OP_0D),
    .out14(OP_0E), .out15(OP_0F), .out16(OP_10), .out17(OP_11), .out18(OP_12), .sel(IR_8_15[7:3]));  // open: out19, out20, out21, out22, out23, out24, out25, out26, out27, out28, out29, out30, out31
  nor nor_1 (T2_T5, T1, T0);
  or or_1 (or_1_out, OP_02, OP_05, OP_06, OP_07, OP_08, OP_09, OP_0A, OP_0B, OP_0C, OP_0D);
  or or_2 (INC_DEC, OP_07, OP_08);
  Multiplexer #(.enable("false")) multiplexer_1 (.in0(1'b1), .in1(or_1_out), .out(Register_ALU), .sel(T2_T5));
  and and_1 (EN_00, T2_T5, OP_00);
  and and_2 (EN_0E, T2_T5, OP_0E);
  and and_3 (EN_01, T2_T5, OP_01);
  and and_4 (EN_07_08, T2_T5, OP_07_08);
  or or_3 (OP_02_0B_0C_0D, OP_02, OP_0B, OP_0C, OP_0D);
  and and_5 (EN_03, T2_T5, OP_03);
  and and_6 (EN_0F, T2_T5, OP_0F);
  and and_7 (EN_09_0A, T2_T5, OP_09_0A);
  and and_8 (EN_10, T2_T5, OP_10);
  and and_9 (EN_04, T2_T5, OP_04);
  and and_10 (EN_05, T2_T5, OP_05);
  and and_11 (EN_02_0B_0C_0D, T2_T5, OP_02_0B_0C_0D);
  and and_12 (EN_11, T2_T5, OP_11);
  or or_4 (OP_07_08, OP_07, OP_08);
  or or_5 (OP_09_0A, OP_09, OP_0A);
  and and_13 (EN_06, T2_T5, OP_06);
  and and_14 (EN_12, T2_T5, OP_12);
  Register #(.width(2)) register_1 (.D(MuxAsel), .en(T2_T5), .Q(register_1_q), .clk(Clock));  // open: clr
  Register #(.width(2)) register_2 (.D(OutCSel_t), .en(T2_T5), .Q(register_2_q), .clk(Clock));  // open: clr
  Register #(.width(2)) register_3 (.D(OutASel_t), .en(T2_T5), .Q(register_3_q), .clk(Clock));  // open: clr
  T0 t0_1 (
    .OutASelOut(register_3_q), .MuxCSel(1'b0), .MuxASelOut(register_1_q), .OutCSelOut(register_2_q), .E(T0),
    .OutAsel(OutAsel), .OutBsel(OutBsel), .Register_Regsel(Register_Regsel),
    .Register_Funsel(Register_Funsel), .MuxCSelOut(MuxCSel), .ALU_Funsel(ALU_Funsel), .ZCNO(ZCNO),
    .MuxAsel(MuxAsel), .MuxBsel(MuxBsel), .OutCSel(OutCSel), .OutDSel(OutDSel),
    .Address_Regsel(Address_Regsel), .Address_Funsel(Address_Funsel), .RAM_Store(RAM_Store),
    .RAM_Load(RAM_Load), .IR_Funsel(IR_Funsel), .IR_Enable(IR_Enable), .IR_LH(IR_LH), .IR_8_15(IR_8_15),
    .IR_0_7(IR_0_7));
  T1 t1_1 (
    .OutASelOut(register_3_q), .MuxCSelOut(1'b0), .MuxASelOut(register_1_q), .OutCSelOut(register_2_q),
    .E(T1), .OutAsel(OutAsel), .OutBsel(OutBsel), .Register_Regsel(Register_Regsel),
    .Register_Funsel(Register_Funsel), .MuxCSel(MuxCSel), .ALU_Funsel(ALU_Funsel), .ZCNO(ZCNO),
    .MuxAsel(MuxAsel), .MuxBsel(MuxBsel), .OutCSel(OutCSel), .OutDSel(OutDSel),
    .Address_Regsel(Address_Regsel), .Address_Funsel(Address_Funsel), .RAM_Store(RAM_Store),
    .RAM_Load(RAM_Load), .IR_Funsel(IR_Funsel), .IR_Enable(IR_Enable), .IR_LH(IR_LH), .IR_8_15(IR_8_15),
    .IR_0_7(IR_0_7));
  OP0 u_OP_00 (
    .T4(T2), .T5(T3), .T6(T4), .T7(T5), .E(EN_00), .Clear(Clear), .OutAsel(OutAsel), .OutBsel(OutBsel),
    .Register_Regsel(Register_Regsel), .Register_Funsel(Register_Funsel), .MuxCSel(MuxCSel),
    .ALU_Funsel(ALU_Funsel), .ZCNO(ZCNO), .MuxAsel(MuxAsel), .MuxBsel(MuxBsel), .OutCSel(OutCSel),
    .OutDSel(OutDSel), .Address_Regsel(Address_Regsel), .Address_Funsel(Address_Funsel),
    .RAM_Store(RAM_Store), .RAM_Load(RAM_Load), .IR_Funsel(IR_Funsel), .IR_Enable(IR_Enable), .IR_LH(IR_LH),
    .IR_8_15(IR_8_15), .IR_0_7(IR_0_7));
  OPcode_0x03_main u_OP_03 (
    .T4(T2), .T5(T3), .T6(T4), .T7(T5), .E(EN_03), .Clear(Clear), .OutAsel(OutAsel), .OutBsel(OutBsel),
    .Register_Regsel(Register_Regsel), .Register_Funsel(Register_Funsel), .MuxCSel(MuxCSel),
    .ALU_Funsel(ALU_Funsel), .ZCNO(ZCNO), .MuxAsel(MuxAsel), .MuxBsel(MuxBsel), .OutCSel(OutCSel),
    .OutDSel(OutDSel), .Address_Regsel(Address_Regsel), .Address_Funsel(Address_Funsel),
    .RAM_Store(RAM_Store), .RAM_Load(RAM_Load), .IR_Funsel(IR_Funsel), .IR_Enable(IR_Enable), .IR_LH(IR_LH),
    .IR_8_15(IR_8_15), .IR_0_7(IR_0_7));
  OPcode_0x05_main u_OP_05 (
    .T4(T2), .T5(T3), .T6(T4), .T7(T5), .E(EN_05), .Clear(Clear), .OutAsel(OutAsel), .OutBsel(OutBsel),
    .Register_Regsel(Register_Regsel), .Register_Funsel(Register_Funsel), .MuxCSel(MuxCSel),
    .ALU_Funsel(ALU_Funsel), .ZCNO(ZCNO), .MuxAsel(MuxAsel), .MuxBsel(MuxBsel), .OutCSel(OutCSel),
    .OutDSel(OutDSel), .Address_Regsel(Address_Regsel), .Address_Funsel(Address_Funsel),
    .RAM_Store(RAM_Store), .RAM_Load(RAM_Load), .IR_Funsel(IR_Funsel), .IR_Enable(IR_Enable), .IR_LH(IR_LH),
    .IR_8_15(IR_8_15), .IR_0_7(IR_0_7));
  OPcode_0x07_0x08_main u_OP_07_08 (
    .T4(T2), .T5(T3), .T6(T4), .T7(T5), .E(EN_07_08), .Clear(Clear), .OutAsel(OutAsel), .OutBsel(OutBsel),
    .Register_Regsel(Register_Regsel), .Register_Funsel(Register_Funsel), .MuxCSel(MuxCSel),
    .ALU_Funsel(ALU_Funsel), .ZCNO(ZCNO), .MuxAsel(MuxAsel), .MuxBsel(MuxBsel), .OutCSel(OutCSel),
    .OutDSel(OutDSel), .Address_Regsel(Address_Regsel), .Address_Funsel(Address_Funsel),
    .RAM_Store(RAM_Store), .RAM_Load(RAM_Load), .IR_Funsel(IR_Funsel), .IR_Enable(IR_Enable), .IR_LH(IR_LH),
    .IR_8_15(IR_8_15), .IR_0_7(IR_0_7));
  OPcode_0x12_main u_OP_12 (
    .T4(T2), .T5(T3), .T6(T4), .T7(T5), .E(EN_12), .Clear(Clear), .OutAsel(OutAsel), .OutBsel(OutBsel),
    .Register_Regsel(Register_Regsel), .Register_Funsel(Register_Funsel), .MuxCSel(MuxCSel),
    .ALU_Funsel(ALU_Funsel), .ZCNO(ZCNO), .MuxAsel(MuxAsel), .MuxBsel(MuxBsel), .OutCSel(OutCSel),
    .OutDSel(OutDSel), .Address_Regsel(Address_Regsel), .Address_Funsel(Address_Funsel),
    .RAM_Store(RAM_Store), .RAM_Load(RAM_Load), .IR_Funsel(IR_Funsel), .IR_Enable(IR_Enable), .IR_LH(IR_LH),
    .IR_8_15(IR_8_15), .IR_0_7(IR_0_7));
  OPcode_0x01_main u_OP_01 (
    .T4(T2), .T5(T3), .T6(T4), .T7(T5), .E(EN_01), .Clear(Clear), .OutAsel(OutAsel), .OutBsel(OutBsel),
    .Register_Regsel(Register_Regsel), .Register_Funsel(Register_Funsel), .MuxCSel(MuxCSel),
    .ALU_Funsel(ALU_Funsel), .ZCNO(ZCNO), .MuxAsel(MuxAsel), .MuxBsel(MuxBsel), .OutCSel(OutCSel),
    .OutDSel(OutDSel), .Address_Regsel(Address_Regsel), .Address_Funsel(Address_Funsel),
    .RAM_Store(RAM_Store), .RAM_Load(RAM_Load), .IR_Funsel(IR_Funsel), .IR_Enable(IR_Enable), .IR_LH(IR_LH),
    .IR_8_15(IR_8_15), .IR_0_7(IR_0_7));
  OPcode_0x02_0x0b_0x0c_0x0d_main u_OP_02_0B_0C_0D (
    .T4(T2), .T5(T3), .T6(T4), .T7(T5), .E(EN_02_0B_0C_0D), .Clear(Clear), .OutAsel(OutAsel),
    .OutBsel(OutBsel), .Register_Regsel(Register_Regsel), .Register_Funsel(Register_Funsel),
    .MuxCSel(MuxCSel), .ALU_Funsel(ALU_Funsel), .ZCNO(ZCNO), .MuxAsel(MuxAsel), .MuxBsel(MuxBsel),
    .OutCSel(OutCSel), .OutDSel(OutDSel), .Address_Regsel(Address_Regsel), .Address_Funsel(Address_Funsel),
    .RAM_Store(RAM_Store), .RAM_Load(RAM_Load), .IR_Funsel(IR_Funsel), .IR_Enable(IR_Enable), .IR_LH(IR_LH),
    .IR_8_15(IR_8_15), .IR_0_7(IR_0_7));
  OPCode_0x06_main u_OP_06 (
    .T4(T2), .T5(T3), .T6(T4), .T7(T5), .E(EN_06), .Clear(Clear), .OutAsel(OutAsel), .OutBsel(OutBsel),
    .Register_Regsel(Register_Regsel), .Register_Funsel(Register_Funsel), .MuxCSel(MuxCSel),
    .ALU_Funsel(ALU_Funsel), .ZCNO(ZCNO), .MuxAsel(MuxAsel), .MuxBsel(MuxBsel), .OutCSel(OutCSel),
    .OutDSel(OutDSel), .Address_Regsel(Address_Regsel), .Address_Funsel(Address_Funsel),
    .RAM_Store(RAM_Store), .RAM_Load(RAM_Load), .IR_Funsel(IR_Funsel), .IR_Enable(IR_Enable), .IR_LH(IR_LH),
    .IR_8_15(IR_8_15), .IR_0_7(IR_0_7));
  OPCode_0x09_0x0a_main u_OP_09_0A (
    .T4(T2), .T5(T3), .T6(T4), .T7(T5), .E(EN_09_0A), .Clear(Clear), .OutAsel(OutAsel), .OutBsel(OutBsel),
    .Register_Regsel(Register_Regsel), .Register_Funsel(Register_Funsel), .MuxCSel(MuxCSel),
    .ALU_Funsel(ALU_Funsel), .ZCNO(ZCNO), .MuxAsel(MuxAsel), .MuxBsel(MuxBsel), .OutCSel(OutCSel),
    .OutDSel(OutDSel), .Address_Regsel(Address_Regsel), .Address_Funsel(Address_Funsel),
    .RAM_Store(RAM_Store), .RAM_Load(RAM_Load), .IR_Funsel(IR_Funsel), .IR_Enable(IR_Enable), .IR_LH(IR_LH),
    .IR_8_15(IR_8_15), .IR_0_7(IR_0_7));
  Opcode_0x04_main u_OP_04 (
    .T4(T2), .T5(T3), .T6(T4), .T7(T5), .E(EN_04), .Clear(Clear), .OutAsel(OutAsel), .OutBsel(OutBsel),
    .Register_Regsel(Register_Regsel), .Register_Funsel(Register_Funsel), .MuxCSel(MuxCSel),
    .ALU_Funsel(ALU_Funsel), .ZCNO(ZCNO), .MuxAsel(MuxAsel), .MuxBsel(MuxBsel), .OutCSel(OutCSel),
    .OutDSel(OutDSel), .Address_Regsel(Address_Regsel), .Address_Funsel(Address_Funsel),
    .RAM_Store(RAM_Store), .RAM_Load(RAM_Load), .IR_Funsel(IR_Funsel), .IR_Enable(IR_Enable), .IR_LH(IR_LH),
    .IR_8_15(IR_8_15), .IR_0_7(IR_0_7));
  Opcode_0x0F_main u_OP_0F (
    .T4(T2), .T5(T3), .T6(T4), .T7(T5), .E(EN_0F), .Clear(Clear), .OutAsel(OutAsel), .OutBsel(OutBsel),
    .Register_Regsel(Register_Regsel), .Register_Funsel(Register_Funsel), .MuxCSel(MuxCSel),
    .ALU_Funsel(ALU_Funsel), .ZCNO(ZCNO), .MuxAsel(MuxAsel), .MuxBsel(MuxBsel), .OutCSel(OutCSel),
    .OutDSel(OutDSel), .Address_Regsel(Address_Regsel), .Address_Funsel(Address_Funsel),
    .RAM_Store(RAM_Store), .RAM_Load(RAM_Load), .IR_Funsel(IR_Funsel), .IR_Enable(IR_Enable), .IR_LH(IR_LH),
    .IR_8_15(IR_8_15), .IR_0_7(IR_0_7));
  OPCode_0x11_main u_OP_11 (
    .T4(T2), .T5(T3), .T6(T4), .T7(T5), .E(EN_11), .Clear(Clear), .OutAsel(OutAsel), .OutBsel(OutBsel),
    .Register_Regsel(Register_Regsel), .Register_Funsel(Register_Funsel), .MuxCSel(MuxCSel),
    .ALU_Funsel(ALU_Funsel), .ZCNO(ZCNO), .MuxAsel(MuxAsel), .MuxBsel(MuxBsel), .OutCSel(OutCSel),
    .OutDSel(OutDSel), .Address_Regsel(Address_Regsel), .Address_Funsel(Address_Funsel),
    .RAM_Store(RAM_Store), .RAM_Load(RAM_Load), .IR_Funsel(IR_Funsel), .IR_Enable(IR_Enable), .IR_LH(IR_LH),
    .IR_8_15(IR_8_15), .IR_0_7(IR_0_7));
  Opcode_0x10_main u_OP_10 (
    .T4(T2), .T5(T3), .T6(T4), .T7(T5), .E(EN_10), .Clear(Clear), .OutAsel(OutAsel), .OutBsel(OutBsel),
    .Register_Regsel(Register_Regsel), .Register_Funsel(Register_Funsel), .MuxCSel(MuxCSel),
    .ALU_Funsel(ALU_Funsel), .ZCNO(ZCNO), .MuxAsel(MuxAsel), .MuxBsel(MuxBsel), .OutCSel(OutCSel),
    .OutDSel(OutDSel), .Address_Regsel(Address_Regsel), .Address_Funsel(Address_Funsel),
    .RAM_Store(RAM_Store), .RAM_Load(RAM_Load), .IR_Funsel(IR_Funsel), .IR_Enable(IR_Enable), .IR_LH(IR_LH),
    .IR_8_15(IR_8_15), .IR_0_7(IR_0_7));
  OPCode_0x0E_main u_OP_0E (
    .T4(T2), .T5(T3), .T6(T4), .T7(T5), .E(EN_0E), .Clear(Clear), .OutAsel(OutAsel), .OutBsel(OutBsel),
    .Register_Regsel(Register_Regsel), .Register_Funsel(Register_Funsel), .MuxCSel(MuxCSel),
    .ALU_Funsel(ALU_Funsel), .ZCNO(ZCNO), .MuxAsel(MuxAsel), .MuxBsel(MuxBsel), .OutCSel(OutCSel),
    .OutDSel(OutDSel), .Address_Regsel(Address_Regsel), .Address_Funsel(Address_Funsel),
    .RAM_Store(RAM_Store), .RAM_Load(RAM_Load), .IR_Funsel(IR_Funsel), .IR_Enable(IR_Enable), .IR_LH(IR_LH),
    .IR_8_15(IR_8_15), .IR_0_7(IR_0_7));

  // Other names for the same wires on the sheet: D3 = IR_8_15[3]; D4 = IR_8_15[4]; D5 = IR_8_15[5]; D6 = IR_8_15[6];
  //   D7 = IR_8_15[7]; D0 = IR_8_15[0]; D1 = IR_8_15[1]; D2 = IR_8_15[2]; T[2:0] = out_22

  // Notes on the sheet:
  //   ENABLE 00
  //   ENABLE 0E
  //   ENABLE 01
  //   ENABLE 07_08
  //   ENABLE
  //   ENABLE 03
  //   ENABLE 0F
  //   ENABLE 09_0A
  //   ENABLE 10
  //   ENABLE 04
  //   ENABLE 05
  //   ENABLE 02_0B_0C_0D
  //   ENABLE 11
  //   ENABLE 06
  //   ENABLE 12
  //   OP_00
  //   OP_03
  //   OP_01
  //   OP_07_08
  //   OP_12
  //   OP_01
  //   OP_02_0B_0C_0D
  //   OP_06
  //   OP_09_0A
  //   OP_04
  //   OP_0F
  //   OP_10
  //   OP_0E
  //   OP_11
endmodule

module OP0 (
  input  [3:0] ZCNO,
  input  [7:0] IR_8_15,
  input  [7:0] IR_0_7,
  input  T4,
  input  T5,
  input  T6,
  input  T7,
  input  E,
  output [1:0] OutAsel,
  output [1:0] OutBsel,
  output [3:0] Register_Regsel,
  output [1:0] Register_Funsel,
  output MuxCSel,
  output [3:0] ALU_Funsel,
  output [1:0] MuxAsel,
  output [1:0] MuxBsel,
  output [1:0] OutCSel,
  output [1:0] OutDSel,
  output [2:0] Address_Regsel,
  output [1:0] Address_Funsel,
  output RAM_Store,
  output RAM_Load,
  output [1:0] IR_Funsel,
  output IR_Enable,
  output IR_LH,
  output Clear
);

  wire and_1_out, and_2_out, Clear_t, IR_Enable_t, IR_LH_t, MuxCSel_t, RAM_Load_t, T4_t, T6_t, T7_t;
  wire [1:0] Address_Funsel_t, IR_Funsel_t, MuxASel_t, MuxBSel_t, OutAsel_t, OutBsel_t, OutCsel_t, OutDsel_t,
       Register_Funsel_t;
  wire [2:0] Address_Regsel_t;
  wire [3:0] ALU_Funsel_t, Register_Regsel_t, ZCNO_t;
  wire [7:0] IR_0_7_t, IR_8_15_t;

  assign OutAsel = E ? OutAsel_t : 2'bz;  // Controlled_Buffer controlled_buffer_1
  assign OutBsel = E ? OutBsel_t : 2'bz;  // Controlled_Buffer controlled_buffer_2
  assign Register_Regsel = E ? Register_Regsel_t : 4'bz;  // Controlled_Buffer controlled_buffer_3
  assign Register_Funsel = E ? Register_Funsel_t : 2'bz;  // Controlled_Buffer controlled_buffer_4
  assign MuxCSel = E ? MuxCSel_t : 1'bz;  // Controlled_Buffer controlled_buffer_5
  assign ALU_Funsel = E ? ALU_Funsel_t : 4'bz;  // Controlled_Buffer controlled_buffer_6
  assign ZCNO_t = E ? ZCNO : 4'bz;  // Controlled_Buffer controlled_buffer_7
  assign MuxAsel = E ? MuxASel_t : 2'bz;  // Controlled_Buffer controlled_buffer_8
  assign MuxBsel = E ? MuxBSel_t : 2'bz;  // Controlled_Buffer controlled_buffer_9
  assign OutCSel = E ? OutCsel_t : 2'bz;  // Controlled_Buffer controlled_buffer_10
  assign OutDSel = E ? OutDsel_t : 2'bz;  // Controlled_Buffer controlled_buffer_11
  assign Address_Regsel = E ? Address_Regsel_t : 3'bz;  // Controlled_Buffer controlled_buffer_12
  assign Address_Funsel = E ? Address_Funsel_t : 2'bz;  // Controlled_Buffer controlled_buffer_13
  assign RAM_Store = E ? 1'b0 : 1'bz;  // Controlled_Buffer controlled_buffer_14
  assign RAM_Load = E ? RAM_Load_t : 1'bz;  // Controlled_Buffer controlled_buffer_15
  assign IR_Funsel = E ? IR_Funsel_t : 2'bz;  // Controlled_Buffer controlled_buffer_16
  assign IR_Enable = E ? IR_Enable_t : 1'bz;  // Controlled_Buffer controlled_buffer_17
  assign IR_LH = E ? IR_LH_t : 1'bz;  // Controlled_Buffer controlled_buffer_18
  assign IR_8_15_t = E ? IR_8_15 : 8'bz;  // Controlled_Buffer controlled_buffer_19
  assign IR_0_7_t = E ? IR_0_7 : 8'bz;  // Controlled_Buffer controlled_buffer_20
  assign T4_t = E ? T4 : 1'bz;  // Controlled_Buffer controlled_buffer_21
  assign Clear_t = E ? T5 : 1'bz;  // Controlled_Buffer controlled_buffer_22
  assign T6_t = E ? T6 : 1'bz;  // Controlled_Buffer controlled_buffer_23
  assign T7_t = E ? T7 : 1'bz;  // Controlled_Buffer controlled_buffer_24
  assign Clear = E ? Clear_t : 1'bz;  // Controlled_Buffer controlled_buffer_25
  Decoder #(.select(2)) decoder_1 (
    .out0(Register_Regsel_t[0]), .out1(Register_Regsel_t[1]), .out2(Register_Regsel_t[2]),
    .out3(Register_Regsel_t[3]), .sel(IR_8_15_t[2:1]), .en(T4_t));
  Multiplexer #(.width(2)) multiplexer_1 (.in1(2'b01), .out(Register_Funsel_t), .sel(T4_t), .en(T4_t));  // open: in0
  Multiplexer #(.width(2)) multiplexer_2 (.in0(2'b00), .in1(2'b01), .out(OutDsel_t), .sel(and_1_out));  // open: en
  and and_1 (and_1_out, T4_t, IR_8_15_t[0]);
  Multiplexer #(.width(3)) multiplexer_3 (
    .in0(3'b000), .in1(3'b010), .out(Address_Regsel_t), .sel(IR_8_15_t[0]), .en(T4_t));
  Multiplexer #(.width(2)) multiplexer_4 (.in1(2'b01), .out(Address_Funsel_t), .sel(and_2_out));  // open: in0, en
  and and_2 (and_2_out, T4_t, IR_8_15_t[0]);
  Multiplexer #(.width(2)) multiplexer_5 (.in0(2'b00), .in1(2'b01), .out(MuxASel_t), .sel(IR_8_15_t[0]), .en(T4_t));
  Multiplexer multiplexer_6 (.in1(1'b1), .out(RAM_Load_t), .sel(T4_t));  // open: in0, en

  // Other names for the same wires on the sheet: Mode = IR_8_15_t[0]; T5_t = Clear_t

  // Notes on the sheet:
  //   OutASel
  //   OutBSel
  //   REGISTER FILE
  //   RegSel
  //   FunSel
  //   OutCSel
  //   OutDSel
  //   ADDRESS REGISTER FILE
  //   RegSel
  //   FunSel
  //   LH
  //   IR
  //   Enable
  //   FunSel
  //   MuxAsel
  //   MuxBsel
  //   MUX
  //   MuxCsel
  //   Store
  //   Load
  //   Clear
endmodule

module T0 (
  input  [1:0] OutASelOut,
  input  MuxCSel,
  input  [3:0] ZCNO,
  input  [1:0] MuxASelOut,
  input  [1:0] OutCSelOut,
  input  [7:0] IR_8_15,
  input  [7:0] IR_0_7,
  input  E,
  output [1:0] OutAsel,
  output [1:0] OutBsel,
  output [3:0] Register_Regsel,
  output [1:0] Register_Funsel,
  output MuxCSelOut,
  output [3:0] ALU_Funsel,
  output [1:0] MuxAsel,
  output [1:0] MuxBsel,
  output [1:0] OutCSel,
  output [1:0] OutDSel,
  output [2:0] Address_Regsel,
  output [1:0] Address_Funsel,
  output RAM_Store,
  output RAM_Load,
  output [1:0] IR_Funsel,
  output IR_Enable,
  output IR_LH
);

  wire [1:0] OutBsel_t, Register_Funsel_t;
  wire [3:0] Register_Regsel_t, ZCNO_t;
  wire [7:0] IR_0_7_t, IR_8_15_t;

  assign OutAsel = E ? OutASelOut : 2'bz;  // Controlled_Buffer controlled_buffer_1
  assign OutBsel = E ? OutBsel_t : 2'bz;  // Controlled_Buffer controlled_buffer_2
  assign Register_Regsel = E ? Register_Regsel_t : 4'bz;  // Controlled_Buffer controlled_buffer_3
  assign Register_Funsel = E ? Register_Funsel_t : 2'bz;  // Controlled_Buffer controlled_buffer_4
  assign MuxCSelOut = E ? MuxCSel : 1'bz;  // Controlled_Buffer controlled_buffer_5
  assign ALU_Funsel = E ? 4'b0000 : 4'bz;  // Controlled_Buffer controlled_buffer_6
  assign ZCNO_t = E ? ZCNO : 4'bz;  // Controlled_Buffer controlled_buffer_7
  assign MuxAsel = E ? MuxASelOut : 2'bz;  // Controlled_Buffer controlled_buffer_8
  assign MuxBsel = E ? 2'b11 : 2'bz;  // Controlled_Buffer controlled_buffer_9
  assign OutCSel = E ? OutCSelOut : 2'bz;  // Controlled_Buffer controlled_buffer_10
  assign OutDSel = E ? 2'b00 : 2'bz;  // Controlled_Buffer controlled_buffer_11
  assign Address_Regsel = E ? 3'b001 : 3'bz;  // Controlled_Buffer controlled_buffer_12
  assign Address_Funsel = E ? 2'b10 : 2'bz;  // Controlled_Buffer controlled_buffer_13
  assign RAM_Store = E ? 1'b0 : 1'bz;  // Controlled_Buffer controlled_buffer_14
  assign RAM_Load = E ? 1'b1 : 1'bz;  // Controlled_Buffer controlled_buffer_15
  assign IR_Funsel = E ? 2'b11 : 2'bz;  // Controlled_Buffer controlled_buffer_16
  assign IR_Enable = E ? 1'b1 : 1'bz;  // Controlled_Buffer controlled_buffer_17
  assign IR_LH = E ? 1'b1 : 1'bz;  // Controlled_Buffer controlled_buffer_18
  assign IR_8_15_t = E ? IR_8_15 : 8'bz;  // Controlled_Buffer controlled_buffer_19
  assign IR_0_7_t = E ? IR_0_7 : 8'bz;  // Controlled_Buffer controlled_buffer_20
endmodule

module T1 (
  input  [1:0] OutASelOut,
  input  MuxCSelOut,
  input  [3:0] ZCNO,
  input  [1:0] MuxASelOut,
  input  [1:0] OutCSelOut,
  input  [7:0] IR_8_15,
  input  [7:0] IR_0_7,
  input  E,
  output [1:0] OutAsel,
  output [1:0] OutBsel,
  output [3:0] Register_Regsel,
  output [1:0] Register_Funsel,
  output MuxCSel,
  output [3:0] ALU_Funsel,
  output [1:0] MuxAsel,
  output [1:0] MuxBsel,
  output [1:0] OutCSel,
  output [1:0] OutDSel,
  output [2:0] Address_Regsel,
  output [1:0] Address_Funsel,
  output RAM_Store,
  output RAM_Load,
  output [1:0] IR_Funsel,
  output IR_Enable,
  output IR_LH
);

  wire [1:0] OutBsel_t, Register_Funsel_t;
  wire [3:0] Register_Regsel_t, ZCNO_t;
  wire [7:0] IR_0_7_t, IR_8_15_t;

  assign OutAsel = E ? OutASelOut : 2'bz;  // Controlled_Buffer controlled_buffer_1
  assign OutBsel = E ? OutBsel_t : 2'bz;  // Controlled_Buffer controlled_buffer_2
  assign Register_Regsel = E ? Register_Regsel_t : 4'bz;  // Controlled_Buffer controlled_buffer_3
  assign Register_Funsel = E ? Register_Funsel_t : 2'bz;  // Controlled_Buffer controlled_buffer_4
  assign MuxCSel = E ? MuxCSelOut : 1'bz;  // Controlled_Buffer controlled_buffer_5
  assign ALU_Funsel = E ? 4'b0000 : 4'bz;  // Controlled_Buffer controlled_buffer_6
  assign ZCNO_t = E ? ZCNO : 4'bz;  // Controlled_Buffer controlled_buffer_7
  assign MuxAsel = E ? MuxASelOut : 2'bz;  // Controlled_Buffer controlled_buffer_8
  assign MuxBsel = E ? 2'b11 : 2'bz;  // Controlled_Buffer controlled_buffer_9
  assign OutCSel = E ? OutCSelOut : 2'bz;  // Controlled_Buffer controlled_buffer_10
  assign OutDSel = E ? 2'b00 : 2'bz;  // Controlled_Buffer controlled_buffer_11
  assign Address_Regsel = E ? 3'b001 : 3'bz;  // Controlled_Buffer controlled_buffer_12
  assign Address_Funsel = E ? 2'b10 : 2'bz;  // Controlled_Buffer controlled_buffer_13
  assign RAM_Store = E ? 1'b0 : 1'bz;  // Controlled_Buffer controlled_buffer_14
  assign RAM_Load = E ? 1'b1 : 1'bz;  // Controlled_Buffer controlled_buffer_15
  assign IR_Funsel = E ? 2'b11 : 2'bz;  // Controlled_Buffer controlled_buffer_16
  assign IR_Enable = E ? 1'b1 : 1'bz;  // Controlled_Buffer controlled_buffer_17
  assign IR_LH = E ? 1'b0 : 1'bz;  // Controlled_Buffer controlled_buffer_18
  assign IR_8_15_t = E ? IR_8_15 : 8'bz;  // Controlled_Buffer controlled_buffer_19
  assign IR_0_7_t = E ? IR_0_7 : 8'bz;  // Controlled_Buffer controlled_buffer_20
endmodule
