// Logisim project OPCode-0x06.circ as structural Verilog: 1 circuit, main circuit main
module main (
  input  [3:0] ZCNO,
  input  [7:0] IR_8_15,
  input  [7:0] IR_0_7,
  input  T4,
  input  T5,
  input  T6,
  input  T7,
  input  E,
  output [1:0] OutAsel,
  output [1:0] OutBsel,
  output [3:0] Register_Regsel,
  output [1:0] Register_Funsel,
  output MuxCSel,
  output [3:0] ALU_Funsel,
  output [1:0] MuxAsel,
  output [1:0] MuxBsel,
  output [1:0] OutCSel,
  output [1:0] OutDSel,
  output [2:0] Address_Regsel,
  output [1:0] Address_Funsel,
  output RAM_Store,
  output RAM_Load,
  output [1:0] IR_Funsel,
  output IR_Enable,
  output IR_LH,
  output Clear
);

  wire and_1_out, and_2_out, and_3_out, and_4_out, and_5_out, Clear_t, decoder_1_out0, decoder_1_out1,
       decoder_1_out2, decoder_1_out3, decoder_2_out0, decoder_2_out1, decoder_2_out2, decoder_2_out3,
       IR_Enable_t, IR_LH_t, MuxCSel_t, nor_1_out, nor_2_out, nor_3_out, nor_4_out, nor_5_out, nor_6_out,
       nor_7_out, nor_8_out, nor_9_out, nor_10_out, nor_11_out, nor_12_out, not_1_out, not_2_out, not_3_out,
       not_4_out, not_5_out, not_6_out, not_7_out, not_8_out, not_9_out, not_10_out, not_11_out, not_12_out,
       not_13_out, not_14_out, not_16_out, not_17_out, not_18_out, not_19_out, or_1_out, or_2_out, or_3_out,
       or_4_out, RAM_Load_t, RAM_Store_t, T4_t, T5_t, T7_t;
  wire [1:0] Address_Funsel_t, controlled_buffer_45_out, controlled_buffer_47_out, controlled_buffer_51_out,
       IR_Funsel_t, MuxASel_t, MuxBSel_t, OutAsel_t, OutBsel_t, OutCsel_t, OutDsel_t, Register_Funsel_t;
  wire [2:0] Address_Regsel_t, controlled_buffer_42_out;
  wire [3:0] controlled_buffer_36_out, Register_Regsel_t, ZCNO_t;
  wire [7:0] IR_0_7_t, IR_8_15_t;

  assign ZCNO_t = E ? ZCNO : 4'bz;  // Controlled_Buffer controlled_buffer_1
  assign IR_8_15_t = E ? IR_8_15 : 8'bz;  // Controlled_Buffer controlled_buffer_2
  assign IR_0_7_t = E ? IR_0_7 : 8'bz;  // Controlled_Buffer controlled_buffer_3
  assign OutAsel = E ? OutAsel_t : 2'bz;  // Controlled_Buffer controlled_buffer_4
  assign OutBsel = E ? OutBsel_t : 2'bz;  // Controlled_Buffer controlled_buffer_5
  assign Register_Regsel = E ? Register_Regsel_t : 4'bz;  // Controlled_Buffer controlled_buffer_6
  assign Register_Funsel = E ? Register_Funsel_t : 2'bz;  // Controlled_Buffer controlled_buffer_7
  assign MuxCSel = E ? MuxCSel_t : 1'bz;  // Controlled_Buffer controlled_buffer_8
  assign ALU_Funsel = E ? 4'b0110 : 4'bz;  // Controlled_Buffer controlled_buffer_9
  assign MuxAsel = E ? MuxASel_t : 2'bz;  // Controlled_Buffer controlled_buffer_10
  assign MuxBsel = E ? MuxBSel_t : 2'bz;  // Controlled_Buffer controlled_buffer_11
  assign OutCSel = E ? OutCsel_t : 2'bz;  // Controlled_Buffer controlled_buffer_12
  assign OutDSel = E ? OutDsel_t : 2'bz;  // Controlled_Buffer controlled_buffer_13
  assign Address_Regsel = E ? Address_Regsel_t : 3'bz;  // Controlled_Buffer controlled_buffer_14
  assign Address_Funsel = E ? Address_Funsel_t : 2'bz;  // Controlled_Buffer controlled_buffer_15
  assign RAM_Store = E ? RAM_Store_t : 1'bz;  // Controlled_Buffer controlled_buffer_16
  assign RAM_Load = E ? RAM_Load_t : 1'bz;  // Controlled_Buffer controlled_buffer_17
  assign IR_Funsel = E ? IR_Funsel_t : 2'bz;  // Controlled_Buffer controlled_buffer_18
  assign IR_Enable = E ? IR_Enable_t : 1'bz;  // Controlled_Buffer controlled_buffer_19
  assign IR_LH = E ? IR_LH_t : 1'bz;  // Controlled_Buffer controlled_buffer_20
  assign T4_t = E ? T4 : 1'bz;  // Controlled_Buffer controlled_buffer_21
  assign T5_t = E ? T5 : 1'bz;  // Controlled_Buffer controlled_buffer_22
  assign Clear_t = E ? T6 : 1'bz;  // Controlled_Buffer controlled_buffer_23
  assign T7_t = E ? T7 : 1'bz;  // Controlled_Buffer controlled_buffer_24
  assign Clear = E ? Clear_t : 1'bz;  // Controlled_Buffer controlled_buffer_25
  assign OutAsel_t = nor_1_out ? 2'b00 : 2'bz;  // Controlled_Buffer controlled_buffer_26
  nor nor_1 (nor_1_out, IR_0_7[2], IR_0_7[3], IR_0_7[4]);
  assign OutAsel_t = nor_2_out ? 2'b01 : 2'bz;  // Controlled_Buffer controlled_buffer_27
  nor nor_2 (nor_2_out, not_1_out, IR_0_7[3], IR_0_7[4]);
  not not_1 (not_1_out, IR_0_7[2]);
  assign OutAsel_t = nor_3_out ? 2'b10 : 2'bz;  // Controlled_Buffer controlled_buffer_28
  nor nor_3 (nor_3_out, IR_0_7[2], not_2_out, IR_0_7[4]);
  not not_2 (not_2_out, IR_0_7[3]);
  assign OutAsel_t = nor_4_out ? 2'b11 : 2'bz;  // Controlled_Buffer controlled_buffer_29
  nor nor_4 (nor_4_out, not_3_out, not_4_out, IR_0_7[4]);
  not not_3 (not_3_out, IR_0_7[2]);
  not not_4 (not_4_out, IR_0_7[3]);
  assign OutAsel_t = IR_0_7[4] ? 2'b00 : 2'bz;  // Controlled_Buffer controlled_buffer_30
  assign OutBsel_t = nor_5_out ? 2'b00 : 2'bz;  // Controlled_Buffer controlled_buffer_31
  nor nor_5 (nor_5_out, IR_0_7[5], IR_0_7[6], IR_0_7[7]);
  assign OutBsel_t = nor_6_out ? 2'b01 : 2'bz;  // Controlled_Buffer controlled_buffer_32
  nor nor_6 (nor_6_out, not_5_out, IR_0_7[6], IR_0_7[7]);
  not not_5 (not_5_out, IR_0_7[5]);
  assign OutBsel_t = nor_7_out ? 2'b10 : 2'bz;  // Controlled_Buffer controlled_buffer_33
  nor nor_7 (nor_7_out, IR_0_7[5], not_6_out, IR_0_7[7]);
  not not_6 (not_6_out, IR_0_7[6]);
  assign OutBsel_t = nor_8_out ? 2'b11 : 2'bz;  // Controlled_Buffer controlled_buffer_34
  nor nor_8 (nor_8_out, not_7_out, not_8_out, IR_0_7[7]);
  not not_7 (not_7_out, IR_0_7[5]);
  not not_8 (not_8_out, IR_0_7[6]);
  assign OutBsel_t = IR_0_7[7] ? 2'b00 : 2'bz;  // Controlled_Buffer controlled_buffer_35
  assign controlled_buffer_36_out = nor_9_out ? 4'b0001 : 4'bz;  // Controlled_Buffer controlled_buffer_36
  nor nor_9 (nor_9_out, IR_8_15[0], IR_8_15[1], IR_8_15[2]);
  assign controlled_buffer_36_out = nor_10_out ? 4'b0010 : 4'bz;  // Controlled_Buffer controlled_buffer_37
  nor nor_10 (nor_10_out, not_9_out, IR_8_15[1], IR_8_15[2]);
  not not_9 (not_9_out, IR_8_15[0]);
  assign controlled_buffer_36_out = nor_11_out ? 4'b0100 : 4'bz;  // Controlled_Buffer controlled_buffer_38
  nor nor_11 (nor_11_out, IR_8_15[0], not_10_out, IR_8_15[2]);
  not not_10 (not_10_out, IR_8_15[1]);
  assign controlled_buffer_36_out = nor_12_out ? 4'b1000 : 4'bz;  // Controlled_Buffer controlled_buffer_39
  nor nor_12 (nor_12_out, not_11_out, not_12_out, IR_8_15[2]);
  not not_11 (not_11_out, IR_8_15[0]);
  not not_12 (not_12_out, IR_8_15[1]);
  not not_13 (not_13_out, IR_8_15[2]);
  and and_1 (and_1_out, not_13_out, T5_t);
  Multiplexer #(.width(4), .enable("false")) multiplexer_1 (
    .in0(4'b0000), .in1(controlled_buffer_36_out), .out(Register_Regsel_t), .sel(and_1_out));
  not not_14 (not_14_out, IR_8_15[2]);
  and and_2 (and_2_out, not_14_out, T5_t);
  assign Register_Funsel_t = and_2_out ? 2'b01 : 2'bz;  // Controlled_Buffer controlled_buffer_40
  assign Address_Funsel_t = IR_8_15[2] ? 2'b01 : 2'bz;  // Controlled_Buffer controlled_buffer_41
  not not_15 (MuxCSel_t, or_1_out);
  or or_1 (or_1_out, IR_0_7[4], IR_0_7[7]);
  assign controlled_buffer_42_out = and_3_out ? 3'b001 : 3'bz;  // Controlled_Buffer controlled_buffer_42
  and and_3 (and_3_out, not_16_out, IR_8_15[2]);
  not not_16 (not_16_out, IR_8_15[1]);
  assign controlled_buffer_42_out = and_4_out ? 3'b010 : 3'bz;  // Controlled_Buffer controlled_buffer_43
  and and_4 (and_4_out, not_17_out, IR_8_15[1], IR_8_15[2]);
  not not_17 (not_17_out, IR_8_15[0]);
  assign controlled_buffer_42_out = and_5_out ? 3'b100 : 3'bz;  // Controlled_Buffer controlled_buffer_44
  and and_5 (and_5_out, IR_8_15[0], IR_8_15[1], IR_8_15[2]);
  Multiplexer #(.width(3), .enable("false")) multiplexer_2 (
    .in0(3'b000), .in1(controlled_buffer_42_out), .out(Address_Regsel_t), .sel(T5_t));
  assign controlled_buffer_45_out = or_2_out ? 2'b00 : 2'bz;  // Controlled_Buffer controlled_buffer_45
  assign controlled_buffer_45_out = decoder_1_out2 ? 2'b01 : 2'bz;  // Controlled_Buffer controlled_buffer_46
  or or_2 (or_2_out, decoder_1_out0, decoder_1_out1);
  Multiplexer #(.width(2), .enable("false")) multiplexer_3 (
    .in0(controlled_buffer_45_out), .in1(controlled_buffer_47_out), .out(OutCsel_t), .sel(IR_0_7[7]));
  assign controlled_buffer_47_out = or_3_out ? 2'b00 : 2'bz;  // Controlled_Buffer controlled_buffer_47
  assign controlled_buffer_45_out = decoder_1_out3 ? 2'b10 : 2'bz;  // Controlled_Buffer controlled_buffer_48
  or or_3 (or_3_out, decoder_2_out0, decoder_2_out1);
  Decoder #(.select(2), .enable("false")) decoder_1 (
    .out0(decoder_1_out0), .out1(decoder_1_out1), .out2(decoder_1_out2), .out3(decoder_1_out3),
    .sel(IR_0_7[3:2]));
  assign controlled_buffer_47_out = decoder_2_out3 ? 2'b10 : 2'bz;  // Controlled_Buffer controlled_buffer_49
  assign controlled_buffer_47_out = decoder_2_out2 ? 2'b01 : 2'bz;  // Controlled_Buffer controlled_buffer_50
  Decoder #(.select(2), .enable("false")) decoder_2 (
    .out0(decoder_2_out0), .out1(decoder_2_out1), .out2(decoder_2_out2), .out3(decoder_2_out3),
    .sel(IR_0_7[6:5]));
  or or_4 (or_4_out, IR_0_7[4], IR_0_7[7]);
  assign controlled_buffer_51_out = or_4_out ? 2'b10 : 2'bz;  // Controlled_Buffer controlled_buffer_51
  assign MuxBSel_t = IR_8_15[2] ? 2'b11 : 2'bz;  // Controlled_Buffer controlled_buffer_52
  not not_18 (not_18_out, or_4_out);
  assign controlled_buffer_51_out = not_18_out ? 2'b11 : 2'bz;  // Controlled_Buffer controlled_buffer_53
  assign MuxBSel_t = not_19_out ? 2'b00 : 2'bz;  // Controlled_Buffer controlled_buffer_54
  not not_19 (not_19_out, IR_8_15[2]);
  Multiplexer #(.width(2), .enable("false")) multiplexer_4 (
    .in0(controlled_buffer_51_out), .in1(2'b11), .out(MuxASel_t), .sel(T5_t));

  // Other names for the same wires on the sheet: SRCREG2[2:0] = IR_0_7[4:2]; DESTREG[2:0] = IR_8_15[2:0];
  //   OPCode[4:0] = IR_8_15[7:3]; SRCREG1[2:0] = IR_0_7[7:5]; T6_t = Clear_t

  // Notes on the sheet:
  //   OutASel
  //   OutBSel
  //   Register-Regsel
  //   Register-Funsel
  //   Address-Funsel
  //   ALU-Funsel
  //   MuxCSel
  //   Addres-Regsel
  //   OutCSel
  //   MuxASel
  //   MuxBSel
endmodule
