// Logisim project OPCode-0x09 0x0a.circ as structural Verilog: 1 circuit, main circuit main
module main (
  input  [3:0] ZCNO,
  input  [7:0] IR_8_15,
  input  [7:0] IR_0_7,
  input  T4,
  input  T5,
  input  T6,
  input  T7,
  input  E,
  output [1:0] OutAsel,
  output [1:0] OutBsel,
  output [3:0] Register_Regsel,
  output [1:0] Register_Funsel,
  output MuxCSel,
  output [3:0] ALU_Funsel,
  output [1:0] MuxAsel,
  output [1:0] MuxBsel,
  output [1:0] OutCSel,
  output [1:0] OutDSel,
  output [2:0] Address_Regsel,
  output [1:0] Address_Funsel,
  output RAM_Store,
  output RAM_Load,
  output [1:0] IR_Funsel,
  output IR_Enable,
  output IR_LH,
  output Clear
);

  wire AND, and_1_out, and_2_out, and_3_out, and_4_out, and_5_out, and_6_out, and_7_out, and_8_out,
       and_9_out, and_10_out, and_11_out, and_12_out, and_13_out, and_14_out, and_15_out, Clear_t,
       decoder_1_out0, decoder_1_out1, decoder_1_out2, decoder_1_out3, decoder_2_out0, decoder_2_out1,
       decoder_2_out2, decoder_2_out3, IR_Enable_t, IR_LH_t, MuxCSel_t, nor_3_out, nor_4_out, nor_5_out,
       nor_6_out, nor_7_out, nor_8_out, nor_9_out, nor_10_out, nor_11_out, nor_12_out, nor_13_out,
       nor_14_out, nor_15_out, not_1_out, not_2_out, not_3_out, not_4_out, not_5_out, not_6_out, not_7_out,
       not_8_out, not_9_out, not_10_out, not_11_out, not_12_out, not_13_out, not_14_out, not_15_out,
       not_16_out, not_17_out, not_18_out, not_19_out, not_20_out, not_22_out, not_23_out, not_24_out,
       not_25_out, OR, or_1_out, or_2_out, or_3_out, or_4_out, T4_t, T5_t, T7_t;
  wire [1:0] Address_Funsel_t, controlled_buffer_31_out, controlled_buffer_48_out, controlled_buffer_51_out,
       IR_Funsel_t, MuxASel_t, MuxBSel_t, OutAsel_t, OutBsel_t, OutCsel_t, OutDsel_t, Register_Funsel_t;
  wire [2:0] Address_Regsel_t, controlled_buffer_45_out;
  wire [3:0] ALU_Funsel_t, Register_Regsel_t, ZCNO_t;
  wire [7:0] IR_0_7_t, IR_8_15_t;

  assign ZCNO_t = E ? ZCNO : 4'bz;  // Controlled_Buffer controlled_buffer_1
  assign IR_8_15_t = E ? IR_8_15 : 8'bz;  // Controlled_Buffer controlled_buffer_2
  assign IR_0_7_t = E ? IR_0_7 : 8'bz;  // Controlled_Buffer controlled_buffer_3
  assign OutAsel = E ? OutAsel_t : 2'bz;  // Controlled_Buffer controlled_buffer_4
  assign OutBsel = E ? OutBsel_t : 2'bz;  // Controlled_Buffer controlled_buffer_5
  assign Register_Regsel = E ? Register_Regsel_t : 4'bz;  // Controlled_Buffer controlled_buffer_6
  assign Register_Funsel = E ? Register_Funsel_t : 2'bz;  // Controlled_Buffer controlled_buffer_7
  assign MuxCSel = E ? MuxCSel_t : 1'bz;  // Controlled_Buffer controlled_buffer_8
  assign ALU_Funsel = E ? ALU_Funsel_t : 4'bz;  // Controlled_Buffer controlled_buffer_9
  assign MuxAsel = E ? MuxASel_t : 2'bz;  // Controlled_Buffer controlled_buffer_10
  assign MuxBsel = E ? MuxBSel_t : 2'bz;  // Controlled_Buffer controlled_buffer_11
  assign OutCSel = E ? OutCsel_t : 2'bz;  // Controlled_Buffer controlled_buffer_12
  assign OutDSel = E ? OutDsel_t : 2'bz;  // Controlled_Buffer controlled_buffer_13
  assign Address_Regsel = E ? Address_Regsel_t : 3'bz;  // Controlled_Buffer controlled_buffer_14
  assign Address_Funsel = E ? Address_Funsel_t : 2'bz;  // Controlled_Buffer controlled_buffer_15
  assign RAM_Store = E ? 1'b0 : 1'bz;  // Controlled_Buffer controlled_buffer_16
  assign RAM_Load = E ? 1'b0 : 1'bz;  // Controlled_Buffer controlled_buffer_17
  assign IR_Funsel = E ? IR_Funsel_t : 2'bz;  // Controlled_Buffer controlled_buffer_18
  assign IR_Enable = E ? IR_Enable_t : 1'bz;  // Controlled_Buffer controlled_buffer_19
  assign IR_LH = E ? IR_LH_t : 1'bz;  // Controlled_Buffer controlled_buffer_20
  assign T4_t = E ? T4 : 1'bz;  // Controlled_Buffer controlled_buffer_21
  assign T5_t = E ? T5 : 1'bz;  // Controlled_Buffer controlled_buffer_22
  assign Clear_t = E ? T6 : 1'bz;  // Controlled_Buffer controlled_buffer_23
  assign T7_t = E ? T7 : 1'bz;  // Controlled_Buffer controlled_buffer_24
  assign Clear = E ? Clear_t : 1'bz;  // Controlled_Buffer controlled_buffer_25
  not not_1 (not_1_out, IR_8_15[6]);
  not not_2 (not_2_out, IR_8_15[3]);
  nor nor_1 (AND, IR_8_15[7], not_1_out, IR_8_15[5], IR_8_15[4], not_2_out);
  not not_3 (not_3_out, IR_8_15[4]);
  not not_4 (not_4_out, IR_8_15[6]);
  nor nor_2 (OR, IR_8_15[7], not_4_out, IR_8_15[5], not_3_out, IR_8_15[3]);
  assign OutAsel_t = nor_3_out ? 2'b00 : 2'bz;  // Controlled_Buffer controlled_buffer_26
  nor nor_3 (nor_3_out, IR_0_7[5], IR_0_7[6], IR_0_7[7]);
  assign OutAsel_t = nor_4_out ? 2'b01 : 2'bz;  // Controlled_Buffer controlled_buffer_27
  nor nor_4 (nor_4_out, not_5_out, IR_0_7[6], IR_0_7[7]);
  not not_5 (not_5_out, IR_0_7[5]);
  assign OutAsel_t = nor_5_out ? 2'b10 : 2'bz;  // Controlled_Buffer controlled_buffer_28
  nor nor_5 (nor_5_out, IR_0_7[5], not_6_out, IR_0_7[7]);
  not not_6 (not_6_out, IR_0_7[6]);
  assign OutAsel_t = nor_6_out ? 2'b11 : 2'bz;  // Controlled_Buffer controlled_buffer_29
  nor nor_6 (nor_6_out, not_7_out, not_8_out, IR_0_7[7]);
  not not_7 (not_7_out, IR_0_7[5]);
  not not_8 (not_8_out, IR_0_7[6]);
  assign OutAsel_t = IR_0_7[7] ? 2'b00 : 2'bz;  // Controlled_Buffer controlled_buffer_30
  not not_9 (not_9_out, IR_0_7[7]);
  and and_1 (and_1_out, not_9_out, IR_0_7[4]);
  nor nor_7 (nor_7_out, IR_0_7[2], IR_0_7[3], IR_0_7[4]);
  nor nor_8 (nor_8_out, not_10_out, IR_0_7[3], IR_0_7[4]);
  not not_10 (not_10_out, IR_0_7[2]);
  nor nor_9 (nor_9_out, IR_0_7[2], not_11_out, IR_0_7[4]);
  not not_11 (not_11_out, IR_0_7[3]);
  nor nor_10 (nor_10_out, not_12_out, not_13_out, IR_0_7[4]);
  not not_12 (not_12_out, IR_0_7[2]);
  not not_13 (not_13_out, IR_0_7[3]);
  assign controlled_buffer_31_out = IR_0_7[4] ? 2'b00 : 2'bz;  // Controlled_Buffer controlled_buffer_31
  not not_14 (not_14_out, and_1_out);
  Multiplexer #(.width(2), .enable("false")) multiplexer_1 (
    .in0(OutAsel_t), .in1(controlled_buffer_31_out), .out(OutBsel_t), .sel(not_14_out));
  assign controlled_buffer_31_out = nor_7_out ? 2'b00 : 2'bz;  // Controlled_Buffer controlled_buffer_32
  assign controlled_buffer_31_out = nor_8_out ? 2'b01 : 2'bz;  // Controlled_Buffer controlled_buffer_33
  assign controlled_buffer_31_out = nor_9_out ? 2'b10 : 2'bz;  // Controlled_Buffer controlled_buffer_34
  assign controlled_buffer_31_out = nor_10_out ? 2'b11 : 2'bz;  // Controlled_Buffer controlled_buffer_35
  not not_15 (not_15_out, T5_t);
  assign Register_Regsel_t = and_2_out ? 4'b0001 : 4'bz;  // Controlled_Buffer controlled_buffer_36
  and and_2 (and_2_out, T5_t, nor_11_out);
  nor nor_11 (nor_11_out, IR_8_15[0], IR_8_15[1], IR_8_15[2]);
  assign Register_Regsel_t = and_3_out ? 4'b0010 : 4'bz;  // Controlled_Buffer controlled_buffer_37
  and and_3 (and_3_out, T5_t, nor_12_out);
  nor nor_12 (nor_12_out, not_16_out, IR_8_15[1], IR_8_15[2]);
  not not_16 (not_16_out, IR_8_15[0]);
  assign Register_Regsel_t = and_4_out ? 4'b0100 : 4'bz;  // Controlled_Buffer controlled_buffer_38
  and and_4 (and_4_out, T5_t, nor_13_out);
  nor nor_13 (nor_13_out, IR_8_15[0], not_17_out, IR_8_15[2]);
  not not_17 (not_17_out, IR_8_15[1]);
  assign Register_Regsel_t = and_5_out ? 4'b1000 : 4'bz;  // Controlled_Buffer controlled_buffer_39
  and and_5 (and_5_out, T5_t, nor_14_out);
  nor nor_14 (nor_14_out, not_18_out, not_19_out, IR_8_15[2]);
  not not_18 (not_18_out, IR_8_15[0]);
  not not_19 (not_19_out, IR_8_15[1]);
  assign Register_Regsel_t = or_1_out ? 4'b0000 : 4'bz;  // Controlled_Buffer controlled_buffer_40
  or or_1 (or_1_out, not_15_out, IR_8_15[2]);
  not not_20 (not_20_out, IR_8_15[2]);
  assign Register_Funsel_t = not_20_out ? 2'b01 : 2'bz;  // Controlled_Buffer controlled_buffer_41
  assign ALU_Funsel_t = AND ? 4'b0111 : 4'bz;  // Controlled_Buffer controlled_buffer_42
  assign ALU_Funsel_t = OR ? 4'b1000 : 4'bz;  // Controlled_Buffer controlled_buffer_43
  or or_2 (or_2_out, IR_0_7[7], IR_0_7[4]);
  not not_21 (MuxCSel_t, or_2_out);
  and and_6 (and_6_out, IR_8_15[2], T5_t);
  assign Address_Funsel_t = and_6_out ? 2'b01 : 2'bz;  // Controlled_Buffer controlled_buffer_44
  and and_7 (and_7_out, T5_t, IR_8_15[2]);
  Multiplexer #(.width(3), .enable("false")) multiplexer_2 (
    .in0(3'b000), .in1(controlled_buffer_45_out), .out(Address_Regsel_t), .sel(and_7_out));
  assign controlled_buffer_45_out = and_8_out ? 3'b001 : 3'bz;  // Controlled_Buffer controlled_buffer_45
  and and_8 (and_8_out, T5_t, and_9_out);
  and and_9 (and_9_out, not_22_out, IR_8_15[2]);
  not not_22 (not_22_out, IR_8_15[1]);
  assign controlled_buffer_45_out = and_10_out ? 3'b010 : 3'bz;  // Controlled_Buffer controlled_buffer_46
  and and_10 (and_10_out, T5_t, and_11_out);
  and and_11 (and_11_out, not_23_out, IR_8_15[1], IR_8_15[2]);
  not not_23 (not_23_out, IR_8_15[0]);
  assign controlled_buffer_45_out = and_12_out ? 3'b100 : 3'bz;  // Controlled_Buffer controlled_buffer_47
  and and_12 (and_12_out, T5_t, and_13_out);
  and and_13 (and_13_out, IR_8_15[0], IR_8_15[1], IR_8_15[2]);
  assign controlled_buffer_48_out = decoder_1_out3 ? 2'b10 : 2'bz;  // Controlled_Buffer controlled_buffer_48
  assign controlled_buffer_48_out = decoder_1_out2 ? 2'b01 : 2'bz;  // Controlled_Buffer controlled_buffer_49
  assign controlled_buffer_48_out = or_3_out ? 2'b00 : 2'bz;  // Controlled_Buffer controlled_buffer_50
  Multiplexer #(.width(2), .enable("false")) multiplexer_3 (
    .in0(controlled_buffer_48_out), .in1(controlled_buffer_51_out), .out(OutCsel_t), .sel(IR_0_7[7]));
  assign controlled_buffer_51_out = decoder_2_out3 ? 2'b10 : 2'bz;  // Controlled_Buffer controlled_buffer_51
  assign controlled_buffer_51_out = decoder_2_out2 ? 2'b01 : 2'bz;  // Controlled_Buffer controlled_buffer_52
  assign controlled_buffer_51_out = or_4_out ? 2'b00 : 2'bz;  // Controlled_Buffer controlled_buffer_53
  or or_3 (or_3_out, decoder_1_out0, decoder_1_out1);
  Decoder #(.select(2), .enable("false")) decoder_1 (
    .out0(decoder_1_out0), .out1(decoder_1_out1), .out2(decoder_1_out2), .out3(decoder_1_out3),
    .sel(IR_0_7[3:2]));
  or or_4 (or_4_out, decoder_2_out0, decoder_2_out1);
  Decoder #(.select(2), .enable("false")) decoder_2 (
    .out0(decoder_2_out0), .out1(decoder_2_out1), .out2(decoder_2_out2), .out3(decoder_2_out3),
    .sel(IR_0_7[6:5]));
  nor nor_15 (nor_15_out, and_14_out, and_15_out);
  not not_24 (not_24_out, IR_8_15[2]);
  assign MuxASel_t = nor_15_out ? 2'b00 : 2'bz;  // Controlled_Buffer controlled_buffer_54
  and and_14 (and_14_out, not_24_out, T5_t);
  assign MuxASel_t = and_14_out ? 2'b11 : 2'bz;  // Controlled_Buffer controlled_buffer_55
  and and_15 (and_15_out, IR_0_7[7], T4_t);
  assign MuxASel_t = and_15_out ? 2'b10 : 2'bz;  // Controlled_Buffer controlled_buffer_56
  not not_25 (not_25_out, IR_8_15[2]);
  assign MuxBSel_t = not_25_out ? 2'b00 : 2'bz;  // Controlled_Buffer controlled_buffer_57
  assign MuxBSel_t = IR_8_15[2] ? 2'b11 : 2'bz;  // Controlled_Buffer controlled_buffer_58

  // Other names for the same wires on the sheet: DESTREG[2:0] = IR_8_15[2:0]; OPCode[4:0] = IR_8_15[7:3];
  //   SRCREG1[2:0] = IR_0_7[7:5]; SRCREG2[2:0] = IR_0_7[4:2]; T6_t = Clear_t

  // Notes on the sheet:
  //   OutASel
  //   Reg and/or Ad (Send Reg to B)
  //   OutBSel
  //   Register-Regsel
  //   Register-Funsel
  //   ALU-Funsel
  //   MuxCSel
  //   Address-Funsel
  //   Addres-Regsel
  //   OutCSel
  //   MuxASel
  //   MuxBSel
endmodule
