// Logisim project OPcode-0x12.circ as structural Verilog: 1 circuit, main circuit main
module main (
  input  [3:0] ZCNO,
  input  [7:0] IR_8_15,
  input  [7:0] IR_0_7,
  input  T4,
  input  T5,
  input  T6,
  input  T7,
  input  E,
  output [1:0] OutAsel,
  output [1:0] OutBsel,
  output [3:0] Register_Regsel,
  output [1:0] Register_Funsel,
  output MuxCSel,
  output [3:0] ALU_Funsel,
  output [1:0] MuxAsel,
  output [1:0] MuxBsel,
  output [1:0] OutCSel,
  output [1:0] OutDSel,
  output [2:0] Address_Regsel,
  output [1:0] Address_Funsel,
  output RAM_Store,
  output RAM_Load,
  output [1:0] IR_Funsel,
  output IR_Enable,
  output IR_LH,
  output Clear
);

  wire Clear_t, IR_Enable_t, IR_LH_t, MuxCSel_t, RAM_Load_t, RAM_Store_t, T4_t, T5_t, T7_t;
  wire [1:0] Address_Funsel_t, IR_Funsel_t, MuxASel_t, MuxBSel_t, OutAsel_t, OutBsel_t, OutCsel_t, OutDsel_t,
       Register_Funsel_t;
  wire [2:0] Address_Regsel_t;
  wire [3:0] ALU_Funsel_t, Register_Regsel_t, ZCNO_t;
  wire [7:0] IR_0_7_t, IR_8_15_t;

  assign ZCNO_t = E ? ZCNO : 4'bz;  // Controlled_Buffer controlled_buffer_1
  assign IR_8_15_t = E ? IR_8_15 : 8'bz;  // Controlled_Buffer controlled_buffer_2
  assign IR_0_7_t = E ? IR_0_7 : 8'bz;  // Controlled_Buffer controlled_buffer_3
  assign OutAsel = E ? OutAsel_t : 2'bz;  // Controlled_Buffer controlled_buffer_4
  assign OutBsel = E ? OutBsel_t : 2'bz;  // Controlled_Buffer controlled_buffer_5
  assign Register_Regsel = E ? Register_Regsel_t : 4'bz;  // Controlled_Buffer controlled_buffer_6
  assign Register_Funsel = E ? Register_Funsel_t : 2'bz;  // Controlled_Buffer controlled_buffer_7
  assign MuxCSel = E ? MuxCSel_t : 1'bz;  // Controlled_Buffer controlled_buffer_8
  assign ALU_Funsel = E ? ALU_Funsel_t : 4'bz;  // Controlled_Buffer controlled_buffer_9
  assign MuxAsel = E ? MuxASel_t : 2'bz;  // Controlled_Buffer controlled_buffer_10
  assign MuxBsel = E ? MuxBSel_t : 2'bz;  // Controlled_Buffer controlled_buffer_11
  assign OutCSel = E ? OutCsel_t : 2'bz;  // Controlled_Buffer controlled_buffer_12
  assign OutDSel = E ? OutDsel_t : 2'bz;  // Controlled_Buffer controlled_buffer_13
  assign Address_Regsel = E ? Address_Regsel_t : 3'bz;  // Controlled_Buffer controlled_buffer_14
  assign Address_Funsel = E ? Address_Funsel_t : 2'bz;  // Controlled_Buffer controlled_buffer_15
  assign RAM_Store = E ? RAM_Store_t : 1'bz;  // Controlled_Buffer controlled_buffer_16
  assign RAM_Load = E ? RAM_Load_t : 1'bz;  // Controlled_Buffer controlled_buffer_17
  assign IR_Funsel = E ? IR_Funsel_t : 2'bz;  // Controlled_Buffer controlled_buffer_18
  assign IR_Enable = E ? IR_Enable_t : 1'bz;  // Controlled_Buffer controlled_buffer_19
  assign IR_LH = E ? IR_LH_t : 1'bz;  // Controlled_Buffer controlled_buffer_20
  assign T4_t = E ? T4 : 1'bz;  // Controlled_Buffer controlled_buffer_21
  assign T5_t = E ? T5 : 1'bz;  // Controlled_Buffer controlled_buffer_22
  assign Clear_t = E ? T6 : 1'bz;  // Controlled_Buffer controlled_buffer_23
  assign T7_t = E ? T7 : 1'bz;  // Controlled_Buffer controlled_buffer_24
  assign Clear = E ? Clear_t : 1'bz;  // Controlled_Buffer controlled_buffer_25
  assign RAM_Store_t = T4_t ? 1'b0 : 1'bz;  // Controlled_Buffer controlled_buffer_26
  assign OutDsel_t = T4_t ? 2'b00 : 2'bz;  // Controlled_Buffer controlled_buffer_27
  assign ALU_Funsel_t = T4_t ? 4'b0000 : 4'bz;  // Controlled_Buffer controlled_buffer_28
  assign MuxCSel_t = T4_t ? 1'b0 : 1'bz;  // Controlled_Buffer controlled_buffer_29
  assign RAM_Load_t = T4_t ? 1'b0 : 1'bz;  // Controlled_Buffer controlled_buffer_30
  assign IR_Enable_t = T4_t ? 1'b0 : 1'bz;  // Controlled_Buffer controlled_buffer_31
  assign Address_Regsel_t = T4_t ? 3'b100 : 3'bz;  // Controlled_Buffer controlled_buffer_32
  assign Address_Funsel_t = T4_t ? 2'b10 : 2'bz;  // Controlled_Buffer controlled_buffer_33
  assign RAM_Store_t = T5_t ? 1'b0 : 1'bz;  // Controlled_Buffer controlled_buffer_34
  assign OutDsel_t = T5_t ? 2'b10 : 2'bz;  // Controlled_Buffer controlled_buffer_35
  assign ALU_Funsel_t = T5_t ? 4'b0000 : 4'bz;  // Controlled_Buffer controlled_buffer_36
  assign MuxCSel_t = T5_t ? 1'b0 : 1'bz;  // Controlled_Buffer controlled_buffer_37
  assign RAM_Load_t = T5_t ? 1'b1 : 1'bz;  // Controlled_Buffer controlled_buffer_38
  assign IR_Enable_t = T5_t ? 1'b0 : 1'bz;  // Controlled_Buffer controlled_buffer_39
  assign MuxBSel_t = T5_t ? 2'b10 : 2'bz;  // Controlled_Buffer controlled_buffer_40
  assign Address_Regsel_t = T5_t ? 3'b001 : 3'bz;  // Controlled_Buffer controlled_buffer_41
  assign Address_Funsel_t = T5_t ? 2'b01 : 2'bz;  // Controlled_Buffer controlled_buffer_42

  // Other names for the same wires on the sheet: T6_t = Clear_t
endmodule
