// Logisim project circular_shift.circ as structural Verilog: 1 circuit, main circuit main
module main (
  input  Carry_In,
  input  [7:0] Input,
  input  Left_Right,
  output Carry_Out,
  output [7:0] Output,
  output Overflow
);

  xor xor_1 (Overflow, Input[7], Output[7]);
  Multiplexer #(.enable("false")) multiplexer_1 (.in0(Carry_In), .in1(Input[1]), .out(Output[0]), .sel(Left_Right));
  Multiplexer #(.enable("false")) multiplexer_2 (.in0(Input[0]), .in1(Input[2]), .out(Output[1]), .sel(Left_Right));
  Multiplexer #(.enable("false")) multiplexer_3 (.in0(Input[1]), .in1(Input[3]), .out(Output[2]), .sel(Left_Right));
  Multiplexer #(.enable("false")) multiplexer_4 (.in0(Input[2]), .in1(Input[4]), .out(Output[3]), .sel(Left_Right));
  Multiplexer #(.enable("false")) multiplexer_5 (.in0(Input[3]), .in1(Input[5]), .out(Output[4]), .sel(Left_Right));
  Multiplexer #(.enable("false")) multiplexer_6 (.in0(Input[4]), .in1(Input[6]), .out(Output[5]), .sel(Left_Right));
  Multiplexer #(.enable("false")) multiplexer_7 (.in0(Input[5]), .in1(Input[7]), .out(Output[6]), .sel(Left_Right));
  Multiplexer #(.enable("false")) multiplexer_8 (.in0(Input[6]), .in1(Carry_In), .out(Output[7]), .sel(Left_Right));
  Multiplexer #(.enable("false")) multiplexer_9 (.in0(Input[7]), .in1(Input[0]), .out(Carry_Out), .sel(Left_Right));
endmodule
